// Logisim project PRESENT.circ as structural Verilog: 22 circuits, main circuit main
module main (
  input  in_1,
  input  in_2,
  input  in_3,
  input  in_4,
  input  in_5,
  input  in_6,
  input  in_7,
  input  in_8,
  input  in_9,
  input  [15:0] in_10,
  input  [31:0] in_11,
  input  [31:0] in_12,
  input  [31:0] in_13,
  input  [31:0] in_14,
  output [3:0] out_15,
  output [31:0] out_16,
  output [31:0] out_17
);

  wire clock_1_out, clock_2_out, counter32_1_out_2, counter32_1_out_3, counter32_1_out_4, counter32_1_out_5,
       counter32_1_out_6, counter32_2_out_2, counter32_2_out_3, counter32_2_out_4, counter32_2_out_5,
       counter32_2_out_6, nor_1_out, nor_2_out, sbox4bit_2_out_5, sbox4bit_2_out_6, sbox4bit_2_out_7,
       sbox4bit_2_out_8;
  wire [3:0] multiplexer_2_out, register_2_q, xor4_1_out_12;
  wire [4:0] multiplexer_1_out, register_1_q;
  wire [4:1] register_1_q_2;
  wire [15:0] keytransform_f_1_out_4, multiplexer_3_out, register_3_q;
  wire [31:0] addroundkey_f_1_out_5, addroundkey_f_1_out_6, keytransform_f_1_out_5, keytransform_f_1_out_6,
       multiplexer_4_out, multiplexer_5_out, multiplexer_6_out, multiplexer_7_out, register_4_q,
       register_5_q, register_6_q, register_7_q;

  Clock clock_1 (.out(clock_1_out));
  Clock clock_2 (.out(clock_2_out));
  XOR4 xor4_1 (
    .in_1(in_1), .in_2(in_2), .in_3(in_3), .in_4(in_4), .in_5(in_6), .in_6(in_7), .in_7(in_8), .in_8(in_9),
    .out_9(xor4_1_out_12[3]), .out_10(xor4_1_out_12[2]), .out_11(xor4_1_out_12[1]), .out_12(xor4_1_out_12[0]));
  Counter32 counter32_1 (
    .in_1(clock_1_out), .out_2(counter32_1_out_2), .out_3(counter32_1_out_3), .out_4(counter32_1_out_4),
    .out_5(counter32_1_out_5), .out_6(counter32_1_out_6));
  Counter32 counter32_2 (
    .in_1(clock_2_out), .out_2(counter32_2_out_2), .out_3(counter32_2_out_3), .out_4(counter32_2_out_4),
    .out_5(counter32_2_out_5), .out_6(counter32_2_out_6));
  nor nor_1 (nor_1_out, counter32_1_out_2, counter32_1_out_3, counter32_1_out_4, counter32_1_out_5, counter32_1_out_6);
  AddRoundKey_F addroundkey_f_1 (
    .in_1(in_11), .in_2(in_12), .in_3(in_13), .in_4(in_14), .out_5(addroundkey_f_1_out_5),
    .out_6(addroundkey_f_1_out_6));
  nor nor_2 (nor_2_out, counter32_2_out_2, counter32_2_out_3, counter32_2_out_4, counter32_2_out_5, counter32_2_out_6);
  Multiplexer #(.width(5), .enable("false")) multiplexer_1 (
    .in0(register_1_q), .in1({in_1, in_2, in_3, in_4, in_5}), .out(multiplexer_1_out), .sel(nor_1_out));
  Multiplexer #(.width(4), .enable("false")) multiplexer_2 (
    .in0(out_15), .in1(xor4_1_out_12), .out(multiplexer_2_out), .sel(nor_1_out));
  Multiplexer #(.width(16), .enable("false")) multiplexer_3 (
    .in0(keytransform_f_1_out_4), .in1(in_10), .out(multiplexer_3_out), .sel(nor_2_out));
  Multiplexer #(.width(32), .enable("false")) multiplexer_4 (
    .in0(keytransform_f_1_out_5), .in1(in_11), .out(multiplexer_4_out), .sel(nor_2_out));
  Multiplexer #(.width(32), .enable("false")) multiplexer_5 (
    .in0(keytransform_f_1_out_6), .in1(in_12), .out(multiplexer_5_out), .sel(nor_2_out));
  Multiplexer #(.width(32), .enable("false")) multiplexer_6 (
    .in0(out_16), .in1(addroundkey_f_1_out_5), .out(multiplexer_6_out), .sel(nor_2_out));
  Multiplexer #(.width(32), .enable("false")) multiplexer_7 (
    .in0(out_17), .in1(addroundkey_f_1_out_6), .out(multiplexer_7_out), .sel(nor_2_out));
  Register #(.width(5)) register_1 (
    .D(multiplexer_1_out), .Q({register_1_q_2, register_1_q[0]}), .clk(clock_1_out));  // open: en, clr
  Register #(.width(4)) register_2 (.D(multiplexer_2_out), .Q(register_2_q), .clk(clock_1_out));  // open: en, clr
  Register #(.width(16)) register_3 (.D(multiplexer_3_out), .Q(register_3_q), .clk(clock_2_out));  // open: en, clr
  Register #(.width(32)) register_4 (.D(multiplexer_4_out), .Q(register_4_q), .clk(clock_2_out));  // open: en, clr
  Register #(.width(32)) register_5 (.D(multiplexer_5_out), .Q(register_5_q), .clk(clock_2_out));  // open: en, clr
  Register #(.width(32)) register_6 (.D(multiplexer_6_out), .Q(register_6_q), .clk(clock_2_out));  // open: en, clr
  Register #(.width(32)) register_7 (.D(multiplexer_7_out), .Q(register_7_q), .clk(clock_2_out));  // open: en, clr
  SBox4Bit sbox4bit_1 (
    .in_1(register_1_q_2[4]), .in_2(register_1_q_2[3]), .in_3(register_1_q_2[2]), .in_4(register_1_q_2[1]),
    .out_5(register_1_q[4]), .out_6(register_1_q[3]), .out_7(register_1_q[2]), .out_8(register_1_q[1]));
  SBox4Bit sbox4bit_2 (
    .in_1(register_2_q[3]), .in_2(register_2_q[2]), .in_3(register_2_q[1]), .in_4(register_2_q[0]),
    .out_5(sbox4bit_2_out_5), .out_6(sbox4bit_2_out_6), .out_7(sbox4bit_2_out_7), .out_8(sbox4bit_2_out_8));
  KeyTransform_F keytransform_f_1 (
    .in_1(register_3_q), .in_2(register_4_q), .in_3(register_5_q), .out_4(keytransform_f_1_out_4),
    .out_5(keytransform_f_1_out_5), .out_6(keytransform_f_1_out_6));
  XOR4 xor4_2 (
    .in_1(register_1_q[4]), .in_2(register_1_q[3]), .in_3(register_1_q[2]), .in_4(register_1_q[1]),
    .in_5(sbox4bit_2_out_5), .in_6(sbox4bit_2_out_6), .in_7(sbox4bit_2_out_7), .in_8(sbox4bit_2_out_8),
    .out_9(out_15[3]), .out_10(out_15[2]), .out_11(out_15[1]), .out_12(out_15[0]));
  SPRLayer_F sprlayer_f_1 (
    .Key(keytransform_f_1_out_5), .Key_2(keytransform_f_1_out_6), .Cipher(register_6_q),
    .Cipher_2(register_7_q), .Output(out_16), .Output_2(out_17));

  // Notes on the sheet:
  //   Main Clock
endmodule

module SBoxA (
  input  in_1,
  input  in_2,
  input  in_3,
  input  in_4,
  output out_5
);

  wire and_1_out, and_2_out, and_3_out, and_4_out, and_5_out, not_1_out, not_2_out, not_3_out, not_4_out;

  not not_1 (not_1_out, in_1);
  not not_2 (not_2_out, in_2);
  not not_3 (not_3_out, in_3);
  not not_4 (not_4_out, in_4);
  and and_1 (and_1_out, not_1_out, not_3_out, not_4_out);
  and and_2 (and_2_out, not_1_out, in_3, in_4);
  and and_3 (and_3_out, not_1_out, in_2, not_4_out);
  and and_4 (and_4_out, in_1, not_2_out, in_4);
  and and_5 (and_5_out, in_1, not_2_out, in_3);
  or or_1 (out_5, and_5_out, and_1_out, and_2_out, and_3_out, and_4_out);
endmodule

module SBoxB (
  input  in_1,
  input  in_2,
  input  in_3,
  input  in_4,
  output out_5
);

  wire and_1_out, and_2_out, and_3_out, and_4_out, and_5_out, not_1_out, not_2_out, not_3_out, not_4_out;

  not not_1 (not_1_out, in_1);
  not not_2 (not_2_out, in_2);
  not not_3 (not_3_out, in_3);
  not not_4 (not_4_out, in_4);
  and and_1 (and_1_out, not_1_out, not_2_out, not_3_out);
  and and_2 (and_2_out, not_2_out, not_3_out, in_4);
  and and_3 (and_3_out, not_2_out, in_3, not_4_out);
  and and_4 (and_4_out, in_1, in_1, in_2, not_3_out);
  and and_5 (and_5_out, not_1_out, in_2, in_3, in_4);
  or or_1 (out_5, and_5_out, and_1_out, and_2_out, and_3_out, and_4_out);
endmodule

module SBoxC (
  input  in_1,
  input  in_2,
  input  in_3,
  input  in_4,
  output out_5
);

  wire and_1_out, and_2_out, and_3_out, and_4_out, and_5_out, not_1_out, not_2_out, not_3_out, not_4_out;

  not not_1 (not_1_out, in_1);
  not not_2 (not_2_out, in_2);
  not not_3 (not_3_out, in_3);
  not not_4 (not_4_out, in_4);
  and and_1 (and_1_out, not_1_out, not_2_out, not_2_out, in_3);
  and and_2 (and_2_out, not_1_out, in_3, not_4_out);
  and and_3 (and_3_out, not_2_out, in_3, not_4_out);
  and and_4 (and_4_out, in_1, in_1, not_2_out, not_3_out);
  and and_5 (and_5_out, in_1, in_2, in_4);
  or or_1 (out_5, and_5_out, and_1_out, and_2_out, and_3_out, and_4_out);
endmodule

module SBoxD (
  input  in_1,
  input  in_2,
  input  in_3,
  input  in_4,
  output out_5
);

  wire and_1_out, and_2_out, and_3_out, and_4_out, and_5_out, and_6_out, not_1_out, not_2_out, not_3_out,
       not_4_out, or_1_out;

  not not_1 (not_1_out, in_1);
  not not_2 (not_2_out, in_2);
  not not_3 (not_3_out, in_3);
  not not_4 (not_4_out, in_4);
  and and_1 (and_1_out, not_1_out, not_2_out, in_4, in_4);
  and and_2 (and_2_out, not_1_out, in_3, in_4);
  and and_3 (and_3_out, in_1, not_2_out, not_4_out);
  and and_4 (and_4_out, in_1, in_3, not_4_out);
  and and_5 (and_5_out, not_1_out, in_2, not_3_out, not_4_out);
  and and_6 (and_6_out, in_1, in_2, not_3_out, in_4);
  or or_1 (or_1_out, and_5_out, and_6_out);
  or or_2 (out_5, or_1_out, and_1_out, and_2_out, and_3_out, and_4_out);
endmodule

module SBox4Bit (
  input  in_1,
  input  in_2,
  input  in_3,
  input  in_4,
  output out_5,
  output out_6,
  output out_7,
  output out_8
);

  SBoxA sboxa_1 (.in_1(in_1), .in_2(in_2), .in_3(in_3), .in_4(in_4), .out_5(out_5));
  SBoxB sboxb_1 (.in_1(in_1), .in_2(in_2), .in_3(in_3), .in_4(in_4), .out_5(out_6));
  SBoxC sboxc_1 (.in_1(in_1), .in_2(in_2), .in_3(in_3), .in_4(in_4), .out_5(out_7));
  SBoxD sboxd_1 (.in_1(in_1), .in_2(in_2), .in_3(in_3), .in_4(in_4), .out_5(out_8));
endmodule

module Sbox64Bit (
  input  [31:0] in_1
);

  SBox4Bit sbox4bit_1 (
    .in_1(in_1[0]), .in_2(in_1[1]), .in_3(in_1[2]), .in_4(in_1[3]));  // open: out_5, out_6, out_7, out_8
  SBox4Bit sbox4bit_2 (
    .in_1(in_1[4]), .in_2(in_1[5]), .in_3(in_1[6]), .in_4(in_1[7]));  // open: out_5, out_6, out_7, out_8
  SBox4Bit sbox4bit_3 (
    .in_1(in_1[8]), .in_2(in_1[9]), .in_3(in_1[10]), .in_4(in_1[11]));  // open: out_5, out_6, out_7, out_8
  SBox4Bit sbox4bit_4 (
    .in_1(in_1[12]), .in_2(in_1[13]), .in_3(in_1[14]), .in_4(in_1[15]));  // open: out_5, out_6, out_7, out_8
  SBox4Bit sbox4bit_5 (
    .in_1(in_1[16]), .in_2(in_1[17]), .in_3(in_1[18]), .in_4(in_1[19]));  // open: out_5, out_6, out_7, out_8
  SBox4Bit sbox4bit_6 (
    .in_1(in_1[20]), .in_2(in_1[21]), .in_3(in_1[22]), .in_4(in_1[23]));  // open: out_5, out_6, out_7, out_8
  SBox4Bit sbox4bit_7 (
    .in_1(in_1[24]), .in_2(in_1[25]), .in_3(in_1[26]), .in_4(in_1[27]));  // open: out_5, out_6, out_7, out_8
  SBox4Bit sbox4bit_8 (
    .in_1(in_1[28]), .in_2(in_1[29]), .in_3(in_1[30]), .in_4(in_1[31]));  // open: out_5, out_6, out_7, out_8
endmodule

module XOR4 (
  input  in_1,
  input  in_2,
  input  in_3,
  input  in_4,
  input  in_5,
  input  in_6,
  input  in_7,
  input  in_8,
  output out_9,
  output out_10,
  output out_11,
  output out_12
);

  xor xor_1 (out_9, in_1, in_5);
  xor xor_2 (out_10, in_2, in_6);
  xor xor_3 (out_11, in_3, in_7);
  xor xor_4 (out_12, in_4, in_8);
endmodule

module XOR16 (
  input  in_1,
  input  in_2,
  input  in_3,
  input  in_4,
  input  in_5,
  input  in_6,
  input  in_7,
  input  in_8,
  input  in_9,
  input  in_10,
  input  in_11,
  input  in_12,
  input  in_13,
  input  in_14,
  input  in_15,
  input  in_16,
  input  in_17,
  input  in_18,
  input  in_19,
  input  in_20,
  input  in_21,
  input  in_22,
  input  in_23,
  input  in_24,
  input  in_25,
  input  in_26,
  input  in_27,
  input  in_28,
  input  in_29,
  input  in_30,
  input  in_31,
  input  in_32,
  output out_33,
  output out_34,
  output out_35,
  output out_36,
  output out_37,
  output out_38,
  output out_39,
  output out_40,
  output out_41,
  output out_42,
  output out_43,
  output out_44,
  output out_45,
  output out_46,
  output out_47,
  output out_48
);

  XOR4 xor4_1 (
    .in_1(in_1), .in_2(in_2), .in_3(in_3), .in_4(in_4), .in_5(in_17), .in_6(in_18), .in_7(in_19),
    .in_8(in_20), .out_9(out_33), .out_10(out_34), .out_11(out_35), .out_12(out_36));
  XOR4 xor4_2 (
    .in_1(in_5), .in_2(in_6), .in_3(in_7), .in_4(in_8), .in_5(in_21), .in_6(in_22), .in_7(in_23),
    .in_8(in_24), .out_9(out_37), .out_10(out_38), .out_11(out_39), .out_12(out_40));
  XOR4 xor4_3 (
    .in_1(in_9), .in_2(in_10), .in_3(in_11), .in_4(in_12), .in_5(in_25), .in_6(in_26), .in_7(in_27),
    .in_8(in_28), .out_9(out_41), .out_10(out_42), .out_11(out_43), .out_12(out_44));
  XOR4 xor4_4 (
    .in_1(in_13), .in_2(in_14), .in_3(in_15), .in_4(in_16), .in_5(in_29), .in_6(in_30), .in_7(in_31),
    .in_8(in_32), .out_9(out_45), .out_10(out_46), .out_11(out_47), .out_12(out_48));
endmodule

module AddRoundKey (
  input  in_1,
  input  in_2,
  input  in_3,
  input  in_4,
  input  in_5,
  input  in_6,
  input  in_7,
  input  in_8,
  input  in_9,
  input  in_10,
  input  in_11,
  input  in_12,
  input  in_13,
  input  in_14,
  input  in_15,
  input  in_16,
  input  in_17,
  input  in_18,
  input  in_19,
  input  in_20,
  input  in_21,
  input  in_22,
  input  in_23,
  input  in_24,
  input  in_25,
  input  in_26,
  input  in_27,
  input  in_28,
  input  in_29,
  input  in_30,
  input  in_31,
  input  in_32,
  input  in_33,
  input  in_34,
  input  in_35,
  input  in_36,
  input  in_37,
  input  in_38,
  input  in_39,
  input  in_40,
  input  in_41,
  input  in_42,
  input  in_43,
  input  in_44,
  input  in_45,
  input  in_46,
  input  in_47,
  input  in_48,
  input  in_49,
  input  in_50,
  input  in_51,
  input  in_52,
  input  in_53,
  input  in_54,
  input  in_55,
  input  in_56,
  input  in_57,
  input  in_58,
  input  in_59,
  input  in_60,
  input  in_61,
  input  in_62,
  input  in_63,
  input  in_64,
  input  in_65,
  input  in_66,
  input  in_67,
  input  in_68,
  input  in_69,
  input  in_70,
  input  in_71,
  input  in_72,
  input  in_73,
  input  in_74,
  input  in_75,
  input  in_76,
  input  in_77,
  input  in_78,
  input  in_79,
  input  in_80,
  input  in_81,
  input  in_82,
  input  in_83,
  input  in_84,
  input  in_85,
  input  in_86,
  input  in_87,
  input  in_88,
  input  in_89,
  input  in_90,
  input  in_91,
  input  in_92,
  input  in_93,
  input  in_94,
  input  in_95,
  input  in_96,
  input  in_97,
  input  in_98,
  input  in_99,
  input  in_100,
  input  in_101,
  input  in_102,
  input  in_103,
  input  in_104,
  input  in_105,
  input  in_106,
  input  in_107,
  input  in_108,
  input  in_109,
  input  in_110,
  input  in_111,
  input  in_112,
  input  in_113,
  input  in_114,
  input  in_115,
  input  in_116,
  input  in_117,
  input  in_118,
  input  in_119,
  input  in_120,
  input  in_121,
  input  in_122,
  input  in_123,
  input  in_124,
  input  in_125,
  input  in_126,
  input  in_127,
  input  in_128,
  output out_129,
  output out_130,
  output out_131,
  output out_132,
  output out_133,
  output out_134,
  output out_135,
  output out_136,
  output out_137,
  output out_138,
  output out_139,
  output out_140,
  output out_141,
  output out_142,
  output out_143,
  output out_144,
  output out_145,
  output out_146,
  output out_147,
  output out_148,
  output out_149,
  output out_150,
  output out_151,
  output out_152,
  output out_153,
  output out_154,
  output out_155,
  output out_156,
  output out_157,
  output out_158,
  output out_159,
  output out_160,
  output out_161,
  output out_162,
  output out_163,
  output out_164,
  output out_165,
  output out_166,
  output out_167,
  output out_168,
  output out_169,
  output out_170,
  output out_171,
  output out_172,
  output out_173,
  output out_174,
  output out_175,
  output out_176,
  output out_177,
  output out_178,
  output out_179,
  output out_180,
  output out_181,
  output out_182,
  output out_183,
  output out_184,
  output out_185,
  output out_186,
  output out_187,
  output out_188,
  output out_189,
  output out_190,
  output out_191,
  output out_192
);

  XOR16 xor16_1 (
    .in_1(in_1), .in_2(in_2), .in_3(in_3), .in_4(in_4), .in_5(in_5), .in_6(in_6), .in_7(in_7), .in_8(in_8),
    .in_9(in_9), .in_10(in_10), .in_11(in_11), .in_12(in_12), .in_13(in_13), .in_14(in_14), .in_15(in_15),
    .in_16(in_16), .in_17(in_65), .in_18(in_66), .in_19(in_67), .in_20(in_68), .in_21(in_69), .in_22(in_70),
    .in_23(in_71), .in_24(in_72), .in_25(in_73), .in_26(in_74), .in_27(in_75), .in_28(in_76), .in_29(in_77),
    .in_30(in_78), .in_31(in_79), .in_32(in_80), .out_33(out_129), .out_34(out_130), .out_35(out_131),
    .out_36(out_132), .out_37(out_133), .out_38(out_134), .out_39(out_135), .out_40(out_136),
    .out_41(out_137), .out_42(out_138), .out_43(out_139), .out_44(out_140), .out_45(out_141),
    .out_46(out_142), .out_47(out_143), .out_48(out_144));
  XOR16 xor16_2 (
    .in_1(in_17), .in_2(in_18), .in_3(in_19), .in_4(in_20), .in_5(in_21), .in_6(in_22), .in_7(in_23),
    .in_8(in_24), .in_9(in_25), .in_10(in_26), .in_11(in_27), .in_12(in_28), .in_13(in_29), .in_14(in_30),
    .in_15(in_31), .in_16(in_32), .in_17(in_81), .in_18(in_82), .in_19(in_83), .in_20(in_84), .in_21(in_85),
    .in_22(in_86), .in_23(in_87), .in_24(in_88), .in_25(in_89), .in_26(in_90), .in_27(in_91), .in_28(in_92),
    .in_29(in_93), .in_30(in_94), .in_31(in_95), .in_32(in_96), .out_33(out_145), .out_34(out_146),
    .out_35(out_147), .out_36(out_148), .out_37(out_149), .out_38(out_150), .out_39(out_151),
    .out_40(out_152), .out_41(out_153), .out_42(out_154), .out_43(out_155), .out_44(out_156),
    .out_45(out_157), .out_46(out_158), .out_47(out_159), .out_48(out_160));
  XOR16 xor16_3 (
    .in_1(in_33), .in_2(in_34), .in_3(in_35), .in_4(in_36), .in_5(in_37), .in_6(in_38), .in_7(in_39),
    .in_8(in_40), .in_9(in_41), .in_10(in_42), .in_11(in_43), .in_12(in_44), .in_13(in_45), .in_14(in_46),
    .in_15(in_47), .in_16(in_48), .in_17(in_97), .in_18(in_98), .in_19(in_99), .in_20(in_100),
    .in_21(in_101), .in_22(in_102), .in_23(in_103), .in_24(in_104), .in_25(in_105), .in_26(in_106),
    .in_27(in_107), .in_28(in_108), .in_29(in_109), .in_30(in_110), .in_31(in_111), .in_32(in_112),
    .out_33(out_161), .out_34(out_162), .out_35(out_163), .out_36(out_164), .out_37(out_165),
    .out_38(out_166), .out_39(out_167), .out_40(out_168), .out_41(out_169), .out_42(out_170),
    .out_43(out_171), .out_44(out_172), .out_45(out_173), .out_46(out_174), .out_47(out_175), .out_48(out_176));
  XOR16 xor16_4 (
    .in_1(in_49), .in_2(in_50), .in_3(in_51), .in_4(in_52), .in_5(in_53), .in_6(in_54), .in_7(in_55),
    .in_8(in_56), .in_9(in_57), .in_10(in_58), .in_11(in_59), .in_12(in_60), .in_13(in_61), .in_14(in_62),
    .in_15(in_63), .in_16(in_64), .in_17(in_113), .in_18(in_114), .in_19(in_115), .in_20(in_116),
    .in_21(in_117), .in_22(in_118), .in_23(in_119), .in_24(in_120), .in_25(in_121), .in_26(in_122),
    .in_27(in_123), .in_28(in_124), .in_29(in_125), .in_30(in_126), .in_31(in_127), .in_32(in_128),
    .out_33(out_177), .out_34(out_178), .out_35(out_179), .out_36(out_180), .out_37(out_181),
    .out_38(out_182), .out_39(out_183), .out_40(out_184), .out_41(out_185), .out_42(out_186),
    .out_43(out_187), .out_44(out_188), .out_45(out_189), .out_46(out_190), .out_47(out_191), .out_48(out_192));
endmodule

module PBox (
  input  [31:0] in_1,
  input  [31:0] in_2,
  input  in_3,
  input  in_4,
  input  in_5,
  input  in_6,
  input  in_7,
  input  in_8,
  input  in_9,
  input  in_10,
  input  in_11,
  input  in_12,
  input  in_13,
  input  in_14,
  input  in_15,
  input  in_16,
  input  in_17,
  input  in_18,
  input  in_19,
  input  in_20,
  input  in_21,
  input  in_22,
  input  in_23,
  input  in_24,
  input  in_25,
  input  in_26,
  input  in_27,
  input  in_28,
  input  in_29,
  input  in_30,
  input  in_31,
  input  in_32,
  input  in_33,
  input  in_34,
  output out_35,
  output out_36,
  output out_37,
  output out_38,
  output out_39,
  output out_40,
  output out_41,
  output out_42,
  output out_43,
  output out_44,
  output out_45,
  output out_46,
  output out_47,
  output out_48,
  output out_49,
  output out_50,
  output out_51,
  output out_52,
  output out_53,
  output out_54,
  output out_55,
  output out_56,
  output out_57,
  output out_58,
  output out_59,
  output out_60,
  output out_61,
  output out_62,
  output out_63,
  output out_64,
  output out_65,
  output out_66,
  output out_67,
  output out_68,
  output out_69,
  output out_70,
  output out_71,
  output out_72,
  output out_73,
  output out_74,
  output out_75,
  output out_76,
  output out_77,
  output out_78,
  output out_79,
  output out_80,
  output out_81,
  output out_82,
  output out_83,
  output out_84,
  output out_85,
  output out_86,
  output out_87,
  output out_88,
  output out_89,
  output out_90,
  output out_91,
  output out_92,
  output out_93,
  output out_94,
  output out_95,
  output out_96,
  output out_97,
  output out_98
);


  assign out_35 = in_1[0];
  assign out_36 = in_1[4];
  assign out_37 = in_1[8];
  assign out_38 = in_1[12];
  assign out_39 = in_1[16];
  assign out_40 = in_1[20];
  assign out_41 = in_1[24];
  assign out_42 = in_1[28];
  assign out_43 = in_3;
  assign out_44 = in_7;
  assign out_45 = in_11;
  assign out_46 = in_15;
  assign out_47 = in_19;
  assign out_48 = in_23;
  assign out_49 = in_27;
  assign out_50 = in_31;
  assign out_51 = in_1[1];
  assign out_52 = in_1[5];
  assign out_53 = in_1[9];
  assign out_54 = in_1[13];
  assign out_55 = in_1[17];
  assign out_56 = in_1[21];
  assign out_57 = in_1[25];
  assign out_58 = in_1[29];
  assign out_59 = in_4;
  assign out_60 = in_8;
  assign out_61 = in_12;
  assign out_62 = in_16;
  assign out_63 = in_20;
  assign out_64 = in_24;
  assign out_65 = in_28;
  assign out_66 = in_32;
  assign out_67 = in_1[2];
  assign out_68 = in_1[6];
  assign out_69 = in_1[10];
  assign out_70 = in_1[14];
  assign out_71 = in_1[18];
  assign out_72 = in_1[22];
  assign out_73 = in_1[26];
  assign out_74 = in_1[30];
  assign out_75 = in_5;
  assign out_76 = in_9;
  assign out_77 = in_13;
  assign out_78 = in_17;
  assign out_79 = in_21;
  assign out_80 = in_25;
  assign out_81 = in_33;
  assign out_82 = in_29;
  assign out_83 = in_1[3];
  assign out_84 = in_1[7];
  assign out_85 = in_1[11];
  assign out_86 = in_1[15];
  assign out_87 = in_1[19];
  assign out_88 = in_1[23];
  assign out_89 = in_1[27];
  assign out_90 = in_1[31];
  assign out_91 = in_6;
  assign out_92 = in_10;
  assign out_93 = in_14;
  assign out_94 = in_18;
  assign out_95 = in_22;
  assign out_96 = in_26;
  assign out_97 = in_30;
  assign out_98 = in_34;
endmodule

module SPRLayer (
  input  in_1,
  input  in_2,
  input  in_3,
  input  in_4,
  input  in_5,
  input  in_6,
  input  in_7,
  input  in_8,
  input  in_9,
  input  in_10,
  input  in_11,
  input  in_12,
  input  in_13,
  input  in_14,
  input  in_15,
  input  in_16,
  input  in_17,
  input  in_18,
  input  in_19,
  input  in_20,
  input  in_21,
  input  in_22,
  input  in_23,
  input  in_24,
  input  in_25,
  input  in_26,
  input  in_27,
  input  in_28,
  input  in_29,
  input  in_30,
  input  in_31,
  input  in_32,
  input  in_33,
  input  in_34,
  input  in_35,
  input  in_36,
  input  in_37,
  input  in_38,
  input  in_39,
  input  in_40,
  input  in_41,
  input  in_42,
  input  in_43,
  input  in_44,
  input  in_45,
  input  in_46,
  input  in_47,
  input  in_48,
  input  in_49,
  input  in_50,
  input  in_51,
  input  in_52,
  input  in_53,
  input  in_54,
  input  in_55,
  input  in_56,
  input  in_57,
  input  in_58,
  input  in_59,
  input  in_60,
  input  in_61,
  input  in_62,
  input  in_63,
  input  in_64,
  input  in_65,
  input  in_66,
  input  in_67,
  input  in_68,
  input  in_69,
  input  in_70,
  input  in_71,
  input  in_72,
  input  in_73,
  input  in_74,
  input  in_75,
  input  in_76,
  input  in_77,
  input  in_78,
  input  in_79,
  input  in_80,
  input  in_81,
  input  in_82,
  input  in_83,
  input  in_84,
  input  in_85,
  input  in_86,
  input  in_87,
  input  in_88,
  input  in_89,
  input  in_90,
  input  in_91,
  input  in_92,
  input  in_93,
  input  in_94,
  input  in_95,
  input  in_96,
  input  in_97,
  input  in_98,
  input  in_99,
  input  in_100,
  input  in_101,
  input  in_102,
  input  in_103,
  input  in_104,
  input  in_105,
  input  in_106,
  input  in_107,
  input  in_108,
  input  in_109,
  input  in_110,
  input  in_111,
  input  in_112,
  input  in_113,
  input  in_114,
  input  in_115,
  input  in_116,
  input  in_117,
  input  in_118,
  input  in_119,
  input  in_120,
  input  in_121,
  input  in_122,
  input  in_123,
  input  in_124,
  input  in_125,
  input  in_126,
  input  in_127,
  input  in_128,
  output out_129,
  output out_130,
  output out_131,
  output out_132,
  output out_133,
  output out_134,
  output out_135,
  output out_136,
  output out_137,
  output out_138,
  output out_139,
  output out_140,
  output out_141,
  output out_142,
  output out_143,
  output out_144,
  output out_145,
  output out_146,
  output out_147,
  output out_148,
  output out_149,
  output out_150,
  output out_151,
  output out_152,
  output out_153,
  output out_154,
  output out_155,
  output out_156,
  output out_157,
  output out_158,
  output out_159,
  output out_160,
  output out_161,
  output out_162,
  output out_163,
  output out_164,
  output out_165,
  output out_166,
  output out_167,
  output out_168,
  output out_169,
  output out_170,
  output out_171,
  output out_172,
  output out_173,
  output out_174,
  output out_175,
  output out_176,
  output out_177,
  output out_178,
  output out_179,
  output out_180,
  output out_181,
  output out_182,
  output out_183,
  output out_184,
  output out_185,
  output out_186,
  output out_187,
  output out_188,
  output out_189,
  output out_190,
  output out_191,
  output out_192
);

  wire pbox_1_p1, pbox_1_p2, pbox_1_p3, pbox_1_p4, pbox_1_p5, pbox_1_p6, pbox_1_p7, pbox_1_p8, pbox_1_p9,
       pbox_1_p10, pbox_1_p11, pbox_1_p12, pbox_1_p13, pbox_1_p14, pbox_1_p15, pbox_1_p16, pbox_1_p17,
       pbox_1_p18, pbox_1_p19, pbox_1_p20, pbox_1_p21, pbox_1_p22, pbox_1_p23, pbox_1_p24, pbox_1_p25,
       pbox_1_p26, pbox_1_p27, pbox_1_p28, pbox_1_p29, pbox_1_p30, pbox_1_p31, pbox_1_p32, pbox_1_p33,
       pbox_1_p34, pbox_1_p35, pbox_1_p36, pbox_1_p37, pbox_1_p38, pbox_1_p39, pbox_1_p40, pbox_1_p41,
       pbox_1_p42, pbox_1_p43, pbox_1_p44, pbox_1_p45, pbox_1_p46, pbox_1_p47, pbox_1_p48, pbox_1_p49,
       pbox_1_p50, pbox_1_p51, pbox_1_p52, pbox_1_p53, pbox_1_p54, pbox_1_p55, pbox_1_p56, pbox_1_p57,
       pbox_1_p58, pbox_1_p59, pbox_1_p60, pbox_1_p61, pbox_1_p62, pbox_1_p63, pbox_1_p64, pbox_1_p65,
       pbox_1_p66, pbox_1_p67, pbox_1_p68, pbox_1_p69, pbox_1_p70, pbox_1_p71, pbox_1_p72, pbox_1_p73,
       pbox_1_p74, pbox_1_p75, pbox_1_p76, pbox_1_p77, pbox_1_p78, pbox_1_p79, pbox_1_p80, pbox_1_p81,
       pbox_1_p82, pbox_1_p83, pbox_1_p84, pbox_1_p85, pbox_1_p86, pbox_1_p87, pbox_1_p88, pbox_1_p89,
       pbox_1_p90, pbox_1_p91, pbox_1_p92, pbox_1_p93, pbox_1_p94, pbox_1_p95, pbox_1_p96, pbox_1_p97,
       pbox_1_p98, pbox_1_p99, pbox_1_p100, pbox_1_p101, pbox_1_p102, pbox_1_p103, pbox_1_p104, pbox_1_p105,
       pbox_1_p106, pbox_1_p107, pbox_1_p108, pbox_1_p109, pbox_1_p110, pbox_1_p111, pbox_1_p112,
       pbox_1_p113, pbox_1_p114, pbox_1_p115, pbox_1_p116, pbox_1_p117, pbox_1_p118, pbox_1_p119,
       pbox_1_p120, pbox_1_p121, pbox_1_p122, pbox_1_p123, pbox_1_p124, pbox_1_p125, pbox_1_p126, pbox_1_p127;

  // PBox pbox_1: pin names not known; wires that end beside it: pbox_1_p1, pbox_1_p2, pbox_1_p3, pbox_1_p4, pbox_1_p5, pbox_1_p6, pbox_1_p7, pbox_1_p8, pbox_1_p9, pbox_1_p10, pbox_1_p11, pbox_1_p12, pbox_1_p13, pbox_1_p14, pbox_1_p15, pbox_1_p16, pbox_1_p17, pbox_1_p18, pbox_1_p19, pbox_1_p20, pbox_1_p21, pbox_1_p22, pbox_1_p23, pbox_1_p24, pbox_1_p25, pbox_1_p26, pbox_1_p27, pbox_1_p28, pbox_1_p29, pbox_1_p30, pbox_1_p31, pbox_1_p32, pbox_1_p33, pbox_1_p34, pbox_1_p35, pbox_1_p36, pbox_1_p37, pbox_1_p38, pbox_1_p39, pbox_1_p40, pbox_1_p41, pbox_1_p42, pbox_1_p43, pbox_1_p44, pbox_1_p45, pbox_1_p46, pbox_1_p47, pbox_1_p48, pbox_1_p49, pbox_1_p50, pbox_1_p51, pbox_1_p52, pbox_1_p53, pbox_1_p54, pbox_1_p55, pbox_1_p56, pbox_1_p57, pbox_1_p58, pbox_1_p59, pbox_1_p60, pbox_1_p61, pbox_1_p62, pbox_1_p63, pbox_1_p64, pbox_1_p65, pbox_1_p66, pbox_1_p67, pbox_1_p68, pbox_1_p69, pbox_1_p70, pbox_1_p71, pbox_1_p72, pbox_1_p73, pbox_1_p74, pbox_1_p75, pbox_1_p76, pbox_1_p77, pbox_1_p78, pbox_1_p79, pbox_1_p80, pbox_1_p81, pbox_1_p82, pbox_1_p83, pbox_1_p84, pbox_1_p85, pbox_1_p86, pbox_1_p87, pbox_1_p88, pbox_1_p89, pbox_1_p90, pbox_1_p91, pbox_1_p92, pbox_1_p93, pbox_1_p94, pbox_1_p95, pbox_1_p96, pbox_1_p97, pbox_1_p98, pbox_1_p99, pbox_1_p100, pbox_1_p101, pbox_1_p102, pbox_1_p103, pbox_1_p104, pbox_1_p105, pbox_1_p106, pbox_1_p107, pbox_1_p108, pbox_1_p109, pbox_1_p110, pbox_1_p111, pbox_1_p112, pbox_1_p113, pbox_1_p114, pbox_1_p115, pbox_1_p116, pbox_1_p117, pbox_1_p118, pbox_1_p119, pbox_1_p120, pbox_1_p121, pbox_1_p122, pbox_1_p123, pbox_1_p124, pbox_1_p125, pbox_1_p126, pbox_1_p127
  AddRoundKey addroundkey_1 (
    .in_1(in_1), .in_2(in_2), .in_3(in_3), .in_4(in_4), .in_5(in_5), .in_6(in_6), .in_7(in_7), .in_8(in_8),
    .in_9(in_9), .in_10(in_10), .in_11(in_11), .in_12(in_12), .in_13(in_13), .in_14(in_14), .in_15(in_15),
    .in_16(in_16), .in_17(in_17), .in_18(in_18), .in_19(in_19), .in_20(in_20), .in_21(in_21), .in_22(in_22),
    .in_23(in_23), .in_24(in_24), .in_25(in_25), .in_26(in_26), .in_27(in_27), .in_28(in_28), .in_29(in_29),
    .in_30(in_30), .in_31(in_31), .in_32(in_32), .in_33(in_33), .in_34(in_34), .in_35(in_35), .in_36(in_36),
    .in_37(in_37), .in_38(in_38), .in_39(in_39), .in_40(in_40), .in_41(in_41), .in_42(in_42), .in_43(in_43),
    .in_44(in_44), .in_45(in_45), .in_46(in_46), .in_47(in_47), .in_48(in_48), .in_49(in_49), .in_50(in_50),
    .in_51(in_51), .in_52(in_52), .in_53(in_53), .in_54(in_54), .in_55(in_55), .in_56(in_56), .in_57(in_57),
    .in_58(in_58), .in_59(in_59), .in_60(in_60), .in_61(in_61), .in_62(in_62), .in_63(in_63), .in_64(in_64),
    .in_65(pbox_1_p64), .in_66(pbox_1_p65), .in_67(pbox_1_p66), .in_68(pbox_1_p67), .in_69(pbox_1_p68),
    .in_70(pbox_1_p69), .in_71(pbox_1_p70), .in_72(pbox_1_p71), .in_73(pbox_1_p72), .in_74(pbox_1_p73),
    .in_75(pbox_1_p74), .in_76(pbox_1_p75), .in_77(pbox_1_p76), .in_78(pbox_1_p77), .in_79(pbox_1_p78),
    .in_80(pbox_1_p79), .in_81(pbox_1_p80), .in_82(pbox_1_p81), .in_83(pbox_1_p82), .in_84(pbox_1_p83),
    .in_85(pbox_1_p84), .in_86(pbox_1_p85), .in_87(pbox_1_p86), .in_88(pbox_1_p87), .in_89(pbox_1_p88),
    .in_90(pbox_1_p89), .in_91(pbox_1_p90), .in_92(pbox_1_p91), .in_93(pbox_1_p92), .in_94(pbox_1_p93),
    .in_95(pbox_1_p94), .in_96(pbox_1_p95), .in_97(pbox_1_p96), .in_98(pbox_1_p97), .in_99(pbox_1_p98),
    .in_100(pbox_1_p99), .in_101(pbox_1_p100), .in_102(pbox_1_p101), .in_103(pbox_1_p102),
    .in_104(pbox_1_p103), .in_105(pbox_1_p104), .in_106(pbox_1_p105), .in_107(pbox_1_p106),
    .in_108(pbox_1_p107), .in_109(pbox_1_p108), .in_110(pbox_1_p109), .in_111(pbox_1_p110),
    .in_112(pbox_1_p111), .in_113(pbox_1_p112), .in_114(pbox_1_p113), .in_115(pbox_1_p114),
    .in_116(pbox_1_p115), .in_117(pbox_1_p116), .in_118(pbox_1_p117), .in_119(pbox_1_p118),
    .in_120(pbox_1_p119), .in_121(pbox_1_p120), .in_122(pbox_1_p121), .in_123(pbox_1_p122),
    .in_124(pbox_1_p123), .in_125(pbox_1_p124), .in_126(pbox_1_p125), .in_127(pbox_1_p126),
    .in_128(pbox_1_p127), .out_129(out_129), .out_130(out_130), .out_131(out_131), .out_132(out_132),
    .out_133(out_133), .out_134(out_134), .out_135(out_135), .out_136(out_136), .out_137(out_137),
    .out_138(out_138), .out_139(out_139), .out_140(out_140), .out_141(out_141), .out_142(out_142),
    .out_143(out_143), .out_144(out_144), .out_145(out_145), .out_146(out_146), .out_147(out_147),
    .out_148(out_148), .out_149(out_149), .out_150(out_150), .out_151(out_151), .out_152(out_152),
    .out_153(out_153), .out_154(out_154), .out_155(out_155), .out_156(out_156), .out_157(out_157),
    .out_158(out_158), .out_159(out_159), .out_160(out_160), .out_161(out_161), .out_162(out_162),
    .out_163(out_163), .out_164(out_164), .out_165(out_165), .out_166(out_166), .out_167(out_167),
    .out_168(out_168), .out_169(out_169), .out_170(out_170), .out_171(out_171), .out_172(out_172),
    .out_173(out_173), .out_174(out_174), .out_175(out_175), .out_176(out_176), .out_177(out_177),
    .out_178(out_178), .out_179(out_179), .out_180(out_180), .out_181(out_181), .out_182(out_182),
    .out_183(out_183), .out_184(out_184), .out_185(out_185), .out_186(out_186), .out_187(out_187),
    .out_188(out_188), .out_189(out_189), .out_190(out_190), .out_191(out_191), .out_192(out_192));
endmodule

module KeyTransform (
  input  in_1,
  input  in_2,
  input  in_3,
  input  in_4,
  input  in_5,
  input  in_6,
  input  in_7,
  input  in_8,
  input  in_9,
  input  in_10,
  input  in_11,
  input  in_12,
  input  in_13,
  input  in_14,
  input  in_15,
  input  in_16,
  input  in_17,
  input  in_18,
  input  in_19,
  input  in_20,
  input  in_21,
  input  in_22,
  input  in_23,
  input  in_24,
  input  in_25,
  input  in_26,
  input  in_27,
  input  in_28,
  input  in_29,
  input  in_30,
  input  in_31,
  input  in_32,
  input  in_33,
  input  in_34,
  input  in_35,
  input  in_36,
  input  in_37,
  input  in_38,
  input  in_39,
  input  in_40,
  input  in_41,
  input  in_42,
  input  in_43,
  input  in_44,
  input  in_45,
  input  in_46,
  input  in_47,
  input  in_48,
  input  in_49,
  input  in_50,
  input  in_51,
  input  in_52,
  input  in_53,
  input  in_54,
  input  in_55,
  input  in_56,
  input  in_57,
  input  in_58,
  input  in_59,
  input  in_60,
  input  in_61,
  input  in_62,
  input  in_63,
  input  in_64,
  input  in_65,
  input  in_66,
  input  in_67,
  input  in_68,
  input  in_69,
  input  in_70,
  input  in_71,
  input  in_72,
  input  in_73,
  input  in_74,
  input  in_75,
  input  in_76,
  input  in_77,
  input  in_78,
  input  in_79,
  input  in_80,
  input  in_81,
  input  in_82,
  input  in_83,
  input  in_84,
  input  in_85
);

  wire keytransstep1_1_out_81, keytransstep1_1_out_82, keytransstep1_1_out_83, keytransstep1_1_out_84,
       keytransstep1_1_out_85, keytransstep1_1_out_86, keytransstep1_1_out_87, keytransstep1_1_out_88,
       keytransstep1_1_out_89, keytransstep1_1_out_90, keytransstep1_1_out_91, keytransstep1_1_out_92,
       keytransstep1_1_out_93, keytransstep1_1_out_94, keytransstep1_1_out_95, keytransstep1_1_out_96,
       keytransstep1_1_out_97, keytransstep1_1_out_98, keytransstep1_1_out_99, keytransstep1_1_out_100,
       keytransstep1_1_out_101, keytransstep1_1_out_102, keytransstep1_1_out_103, keytransstep1_1_out_104,
       keytransstep1_1_out_105, keytransstep1_1_out_106, keytransstep1_1_out_107, keytransstep1_1_out_108,
       keytransstep1_1_out_109, keytransstep1_1_out_110, keytransstep1_1_out_111, keytransstep1_1_out_112,
       keytransstep1_1_out_113, keytransstep1_1_out_114, keytransstep1_1_out_115, keytransstep1_1_out_116,
       keytransstep1_1_out_117, keytransstep1_1_out_118, keytransstep1_1_out_119, keytransstep1_1_out_120,
       keytransstep1_1_out_121, keytransstep1_1_out_122, keytransstep1_1_out_123, keytransstep1_1_out_124,
       keytransstep1_1_out_125, keytransstep1_1_out_126, keytransstep1_1_out_127, keytransstep1_1_out_128,
       keytransstep1_1_out_129, keytransstep1_1_out_130, keytransstep1_1_out_131, keytransstep1_1_out_132,
       keytransstep1_1_out_133, keytransstep1_1_out_134, keytransstep1_1_out_135, keytransstep1_1_out_136,
       keytransstep1_1_out_137, keytransstep1_1_out_138, keytransstep1_1_out_139, keytransstep1_1_out_140,
       keytransstep1_1_out_141, keytransstep1_1_out_142, keytransstep1_1_out_143, keytransstep1_1_out_144,
       keytransstep1_1_out_145, keytransstep1_1_out_146, keytransstep1_1_out_147, keytransstep1_1_out_148,
       keytransstep1_1_out_149, keytransstep1_1_out_150, keytransstep1_1_out_151, keytransstep1_1_out_152,
       keytransstep1_1_out_153, keytransstep1_1_out_154, keytransstep1_1_out_155, keytransstep1_1_out_156,
       keytransstep1_1_out_157, keytransstep1_1_out_158, keytransstep1_1_out_159, keytransstep1_1_out_160,
       sbox4bit_1_out_5, sbox4bit_1_out_6, sbox4bit_1_out_7, sbox4bit_1_out_8, xor5_1_out_11, xor5_1_out_12,
       xor5_1_out_13, xor5_1_out_14, xor5_1_out_15;

  KeyTransStep1 keytransstep1_1 (
    .in_1(in_1), .in_2(in_2), .in_3(in_3), .in_4(in_4), .in_5(in_5), .in_6(in_6), .in_7(in_7), .in_8(in_8),
    .in_9(in_9), .in_10(in_10), .in_11(in_11), .in_12(in_12), .in_13(in_13), .in_14(in_14), .in_15(in_15),
    .in_16(in_16), .in_17(in_17), .in_18(in_18), .in_19(in_19), .in_20(in_20), .in_21(in_21), .in_22(in_22),
    .in_23(in_23), .in_24(in_24), .in_25(in_25), .in_26(in_26), .in_27(in_27), .in_28(in_28), .in_29(in_29),
    .in_30(in_30), .in_31(in_31), .in_32(in_32), .in_33(in_33), .in_34(in_34), .in_35(in_35), .in_36(in_36),
    .in_37(in_37), .in_38(in_38), .in_39(in_39), .in_40(in_40), .in_41(in_41), .in_42(in_42), .in_43(in_43),
    .in_44(in_44), .in_45(in_45), .in_46(in_46), .in_47(in_47), .in_48(in_48), .in_49(in_49), .in_50(in_50),
    .in_51(in_51), .in_52(in_52), .in_53(in_53), .in_54(in_54), .in_55(in_55), .in_56(in_56), .in_57(in_57),
    .in_58(in_58), .in_59(in_59), .in_60(in_60), .in_61(in_61), .in_62(in_62), .in_63(in_63), .in_64(in_64),
    .in_65(in_65), .in_66(in_66), .in_67(in_67), .in_68(in_68), .in_69(in_69), .in_70(in_70), .in_71(in_71),
    .in_72(in_72), .in_73(in_73), .in_74(in_74), .in_75(in_75), .in_76(in_76), .in_77(in_77), .in_78(in_78),
    .in_79(in_79), .in_80(in_80), .out_81(keytransstep1_1_out_81), .out_82(keytransstep1_1_out_82),
    .out_83(keytransstep1_1_out_83), .out_84(keytransstep1_1_out_84), .out_85(keytransstep1_1_out_85),
    .out_86(keytransstep1_1_out_86), .out_87(keytransstep1_1_out_87), .out_88(keytransstep1_1_out_88),
    .out_89(keytransstep1_1_out_89), .out_90(keytransstep1_1_out_90), .out_91(keytransstep1_1_out_91),
    .out_92(keytransstep1_1_out_92), .out_93(keytransstep1_1_out_93), .out_94(keytransstep1_1_out_94),
    .out_95(keytransstep1_1_out_95), .out_96(keytransstep1_1_out_96), .out_97(keytransstep1_1_out_97),
    .out_98(keytransstep1_1_out_98), .out_99(keytransstep1_1_out_99), .out_100(keytransstep1_1_out_100),
    .out_101(keytransstep1_1_out_101), .out_102(keytransstep1_1_out_102), .out_103(keytransstep1_1_out_103),
    .out_104(keytransstep1_1_out_104), .out_105(keytransstep1_1_out_105), .out_106(keytransstep1_1_out_106),
    .out_107(keytransstep1_1_out_107), .out_108(keytransstep1_1_out_108), .out_109(keytransstep1_1_out_109),
    .out_110(keytransstep1_1_out_110), .out_111(keytransstep1_1_out_111), .out_112(keytransstep1_1_out_112),
    .out_113(keytransstep1_1_out_113), .out_114(keytransstep1_1_out_114), .out_115(keytransstep1_1_out_115),
    .out_116(keytransstep1_1_out_116), .out_117(keytransstep1_1_out_117), .out_118(keytransstep1_1_out_118),
    .out_119(keytransstep1_1_out_119), .out_120(keytransstep1_1_out_120), .out_121(keytransstep1_1_out_121),
    .out_122(keytransstep1_1_out_122), .out_123(keytransstep1_1_out_123), .out_124(keytransstep1_1_out_124),
    .out_125(keytransstep1_1_out_125), .out_126(keytransstep1_1_out_126), .out_127(keytransstep1_1_out_127),
    .out_128(keytransstep1_1_out_128), .out_129(keytransstep1_1_out_129), .out_130(keytransstep1_1_out_130),
    .out_131(keytransstep1_1_out_131), .out_132(keytransstep1_1_out_132), .out_133(keytransstep1_1_out_133),
    .out_134(keytransstep1_1_out_134), .out_135(keytransstep1_1_out_135), .out_136(keytransstep1_1_out_136),
    .out_137(keytransstep1_1_out_137), .out_138(keytransstep1_1_out_138), .out_139(keytransstep1_1_out_139),
    .out_140(keytransstep1_1_out_140), .out_141(keytransstep1_1_out_141), .out_142(keytransstep1_1_out_142),
    .out_143(keytransstep1_1_out_143), .out_144(keytransstep1_1_out_144), .out_145(keytransstep1_1_out_145),
    .out_146(keytransstep1_1_out_146), .out_147(keytransstep1_1_out_147), .out_148(keytransstep1_1_out_148),
    .out_149(keytransstep1_1_out_149), .out_150(keytransstep1_1_out_150), .out_151(keytransstep1_1_out_151),
    .out_152(keytransstep1_1_out_152), .out_153(keytransstep1_1_out_153), .out_154(keytransstep1_1_out_154),
    .out_155(keytransstep1_1_out_155), .out_156(keytransstep1_1_out_156), .out_157(keytransstep1_1_out_157),
    .out_158(keytransstep1_1_out_158), .out_159(keytransstep1_1_out_159), .out_160(keytransstep1_1_out_160));
  SBox4Bit sbox4bit_1 (
    .in_1(keytransstep1_1_out_81), .in_2(keytransstep1_1_out_82), .in_3(keytransstep1_1_out_83),
    .in_4(keytransstep1_1_out_84), .out_5(sbox4bit_1_out_5), .out_6(sbox4bit_1_out_6),
    .out_7(sbox4bit_1_out_7), .out_8(sbox4bit_1_out_8));
  XOR5 xor5_1 (
    .in_1(keytransstep1_1_out_140), .in_2(keytransstep1_1_out_141), .in_3(keytransstep1_1_out_142),
    .in_4(keytransstep1_1_out_143), .in_5(keytransstep1_1_out_144), .in_6(in_81), .in_7(in_82), .in_8(in_83),
    .in_9(in_84), .in_10(in_85), .out_11(xor5_1_out_11), .out_12(xor5_1_out_12), .out_13(xor5_1_out_13),
    .out_14(xor5_1_out_14), .out_15(xor5_1_out_15));
endmodule

module KeyTransStep1 (
  input  in_1,
  input  in_2,
  input  in_3,
  input  in_4,
  input  in_5,
  input  in_6,
  input  in_7,
  input  in_8,
  input  in_9,
  input  in_10,
  input  in_11,
  input  in_12,
  input  in_13,
  input  in_14,
  input  in_15,
  input  in_16,
  input  in_17,
  input  in_18,
  input  in_19,
  input  in_20,
  input  in_21,
  input  in_22,
  input  in_23,
  input  in_24,
  input  in_25,
  input  in_26,
  input  in_27,
  input  in_28,
  input  in_29,
  input  in_30,
  input  in_31,
  input  in_32,
  input  in_33,
  input  in_34,
  input  in_35,
  input  in_36,
  input  in_37,
  input  in_38,
  input  in_39,
  input  in_40,
  input  in_41,
  input  in_42,
  input  in_43,
  input  in_44,
  input  in_45,
  input  in_46,
  input  in_47,
  input  in_48,
  input  in_49,
  input  in_50,
  input  in_51,
  input  in_52,
  input  in_53,
  input  in_54,
  input  in_55,
  input  in_56,
  input  in_57,
  input  in_58,
  input  in_59,
  input  in_60,
  input  in_61,
  input  in_62,
  input  in_63,
  input  in_64,
  input  in_65,
  input  in_66,
  input  in_67,
  input  in_68,
  input  in_69,
  input  in_70,
  input  in_71,
  input  in_72,
  input  in_73,
  input  in_74,
  input  in_75,
  input  in_76,
  input  in_77,
  input  in_78,
  input  in_79,
  input  in_80,
  output out_81,
  output out_82,
  output out_83,
  output out_84,
  output out_85,
  output out_86,
  output out_87,
  output out_88,
  output out_89,
  output out_90,
  output out_91,
  output out_92,
  output out_93,
  output out_94,
  output out_95,
  output out_96,
  output out_97,
  output out_98,
  output out_99,
  output out_100,
  output out_101,
  output out_102,
  output out_103,
  output out_104,
  output out_105,
  output out_106,
  output out_107,
  output out_108,
  output out_109,
  output out_110,
  output out_111,
  output out_112,
  output out_113,
  output out_114,
  output out_115,
  output out_116,
  output out_117,
  output out_118,
  output out_119,
  output out_120,
  output out_121,
  output out_122,
  output out_123,
  output out_124,
  output out_125,
  output out_126,
  output out_127,
  output out_128,
  output out_129,
  output out_130,
  output out_131,
  output out_132,
  output out_133,
  output out_134,
  output out_135,
  output out_136,
  output out_137,
  output out_138,
  output out_139,
  output out_140,
  output out_141,
  output out_142,
  output out_143,
  output out_144,
  output out_145,
  output out_146,
  output out_147,
  output out_148,
  output out_149,
  output out_150,
  output out_151,
  output out_152,
  output out_153,
  output out_154,
  output out_155,
  output out_156,
  output out_157,
  output out_158,
  output out_159,
  output out_160
);


  assign out_81 = in_62;
  assign out_82 = in_63;
  assign out_83 = in_64;
  assign out_84 = in_65;
  assign out_85 = in_66;
  assign out_86 = in_67;
  assign out_87 = in_68;
  assign out_88 = in_69;
  assign out_89 = in_70;
  assign out_90 = in_71;
  assign out_91 = in_72;
  assign out_92 = in_73;
  assign out_93 = in_74;
  assign out_94 = in_75;
  assign out_95 = in_76;
  assign out_96 = in_77;
  assign out_97 = in_78;
  assign out_98 = in_79;
  assign out_99 = in_80;
  assign out_100 = in_1;
  assign out_101 = in_2;
  assign out_102 = in_3;
  assign out_103 = in_4;
  assign out_104 = in_5;
  assign out_105 = in_6;
  assign out_106 = in_7;
  assign out_107 = in_8;
  assign out_108 = in_9;
  assign out_109 = in_10;
  assign out_110 = in_11;
  assign out_111 = in_12;
  assign out_112 = in_13;
  assign out_113 = in_14;
  assign out_114 = in_15;
  assign out_115 = in_16;
  assign out_116 = in_17;
  assign out_117 = in_18;
  assign out_118 = in_19;
  assign out_119 = in_20;
  assign out_120 = in_21;
  assign out_121 = in_22;
  assign out_122 = in_23;
  assign out_123 = in_24;
  assign out_124 = in_25;
  assign out_125 = in_26;
  assign out_126 = in_27;
  assign out_127 = in_28;
  assign out_128 = in_29;
  assign out_129 = in_30;
  assign out_130 = in_31;
  assign out_131 = in_32;
  assign out_132 = in_33;
  assign out_133 = in_34;
  assign out_134 = in_35;
  assign out_135 = in_36;
  assign out_136 = in_37;
  assign out_137 = in_38;
  assign out_138 = in_39;
  assign out_139 = in_40;
  assign out_140 = in_41;
  assign out_141 = in_42;
  assign out_142 = in_43;
  assign out_143 = in_44;
  assign out_144 = in_45;
  assign out_145 = in_46;
  assign out_146 = in_47;
  assign out_147 = in_48;
  assign out_148 = in_49;
  assign out_149 = in_50;
  assign out_150 = in_51;
  assign out_151 = in_52;
  assign out_152 = in_53;
  assign out_153 = in_54;
  assign out_154 = in_55;
  assign out_155 = in_56;
  assign out_156 = in_57;
  assign out_157 = in_58;
  assign out_158 = in_59;
  assign out_159 = in_60;
  assign out_160 = in_61;
endmodule

module XOR5 (
  input  in_1,
  input  in_2,
  input  in_3,
  input  in_4,
  input  in_5,
  input  in_6,
  input  in_7,
  input  in_8,
  input  in_9,
  input  in_10,
  output out_11,
  output out_12,
  output out_13,
  output out_14,
  output out_15
);

  xor xor_1 (out_11, in_1, in_6);
  xor xor_2 (out_12, in_2, in_7);
  xor xor_3 (out_13, in_3, in_8);
  xor xor_4 (out_14, in_4, in_9);
  xor xor_5 (out_15, in_5, in_10);
endmodule

module Counter32 (
  input  in_1,
  output out_2,
  output out_3,
  output out_4,
  output out_5,
  output out_6
);

  wire and_1_out, and_2_out, and_3_out;

  T_Flip_Flop A (.clk(in_1), .T(1'b1), .Q(out_6), .en(1'b1));  // open: Qn, preset, reset
  T_Flip_Flop B (.clk(in_1), .T(out_6), .Q(out_5), .en(1'b1));  // open: Qn, preset, reset
  and and_1 (and_1_out, out_5, out_6);
  T_Flip_Flop C (.clk(in_1), .T(and_1_out), .Q(out_4), .en(1'b1));  // open: Qn, preset, reset
  and and_2 (and_2_out, out_4, and_1_out);
  T_Flip_Flop D (.clk(in_1), .T(and_2_out), .Q(out_3), .en(1'b1));  // open: Qn, preset, reset
  and and_3 (and_3_out, out_3, and_2_out);
  T_Flip_Flop E (.clk(in_1), .T(and_3_out), .Q(out_2), .en(1'b1));  // open: Qn, preset, reset
endmodule

module AddRoundKey_F (
  input  [31:0] in_1,
  input  [31:0] in_2,
  input  [31:0] in_3,
  input  [31:0] in_4,
  output [31:0] out_5,
  output [31:0] out_6
);

  assign out_5 = in_1 ^ in_3;  // XOR_Gate xor_1, 32 bits wide
  assign out_6 = in_2 ^ in_4;  // XOR_Gate xor_2, 32 bits wide
endmodule

module PBox_F (
  input  [31:0] in_1,
  input  [31:0] in_2,
  output [31:0] out_3,
  output [31:0] out_4
);


  assign out_3 = {in_2[29], in_2[25], in_2[21], in_2[17], in_2[13], in_2[9], in_2[5], in_2[1], in_1[29], in_1[25], in_1[21], in_1[17], in_1[13], in_1[9], in_1[5], in_1[1], in_2[28], in_2[24], in_2[20], in_2[16], in_2[12], in_2[8], in_2[4], in_2[0], in_1[28], in_1[24], in_1[20], in_1[16], in_1[12], in_1[8], in_1[4], in_1[0]};
  assign out_4 = {in_2[31], in_2[27], in_2[23], in_2[19], in_2[15], in_2[11], in_2[7], in_2[3], in_1[31], in_1[27], in_1[23], in_1[19], in_1[15], in_1[11], in_1[7], in_1[3], in_2[30], in_2[26], in_2[22], in_2[18], in_2[14], in_2[10], in_2[6], in_2[2], in_1[30], in_1[26], in_1[22], in_1[18], in_1[14], in_1[10], in_1[6], in_1[2]};

  // Other names for the same wires on the sheet: _0 = in_1[0]; _1 = in_1[4]; _2 = in_1[8]; _3 = in_1[12];
  //   _4 = in_1[16]; _5 = in_1[20]; _6 = in_1[24]; _7 = in_1[28]; _8 = in_2[0]; _9 = in_2[4]; _10 = in_2[8];
  //   _11 = in_2[12]; _12 = in_2[16]; _13 = in_2[20]; _14 = in_2[24]; _15 = in_2[28]; _16 = in_1[1]; _17 = in_1[5];
  //   _18 = in_1[9]; _19 = in_1[13]; _20 = in_1[17]; _21 = in_1[21]; _22 = in_1[25]; _23 = in_1[29]; _24 = in_2[1];
  //   _25 = in_2[5]; _26 = in_2[9]; _27 = in_2[13]; _28 = in_2[17]; _29 = in_2[21]; _30 = in_2[25]; _31 = in_2[29];
  //   _32 = in_1[2]; _33 = in_1[6]; _34 = in_1[10]; _35 = in_1[14]; _36 = in_1[18]; _37 = in_1[22]; _38 = in_1[26];
  //   _39 = in_1[30]; _40 = in_2[2]; _41 = in_2[6]; _42 = in_2[10]; _43 = in_2[14]; _44 = in_2[18]; _45 = in_2[22];
  //   _46 = in_2[26]; _47 = in_2[30]; _48 = in_1[3]; _49 = in_1[7]; _50 = in_1[11]; _51 = in_1[15]; _52 = in_1[19];
  //   _53 = in_1[23]; _54 = in_1[27]; _55 = in_1[31]; _56 = in_2[3]; _57 = in_2[7]; _58 = in_2[11]; _59 = in_2[15];
  //   _60 = in_2[19]; _61 = in_2[23]; _62 = in_2[27]; _63 = in_2[31]
endmodule

module SBox4Bit_F (
  input  in_1,
  input  in_2,
  input  in_3,
  input  in_4,
  output out_5,
  output out_6,
  output out_7,
  output out_8
);

  SBoxD sboxd_1 (.in_1(in_1), .in_2(in_2), .in_3(in_3), .in_4(in_4), .out_5(out_5));
  SBoxC sboxc_1 (.in_1(in_1), .in_2(in_2), .in_3(in_3), .in_4(in_4), .out_5(out_6));
  SBoxB sboxb_1 (.in_1(in_1), .in_2(in_2), .in_3(in_3), .in_4(in_4), .out_5(out_7));
  SBoxA sboxa_1 (.in_1(in_1), .in_2(in_2), .in_3(in_3), .in_4(in_4), .out_5(out_8));
endmodule

module SBox64Bit_F (
  input  [31:0] in_1,
  input  [31:0] in_2,
  output [31:0] out_3,
  output [31:0] out_4
);

  SBox4Bit_F sbox4bit_f_1 (
    .in_1(in_1[0]), .in_2(in_1[1]), .in_3(in_1[2]), .in_4(in_1[3]), .out_5(out_3[0]), .out_6(out_3[1]),
    .out_7(out_3[2]), .out_8(out_3[3]));
  SBox4Bit_F sbox4bit_f_2 (
    .in_1(in_1[4]), .in_2(in_1[5]), .in_3(in_1[6]), .in_4(in_1[7]), .out_5(out_3[4]), .out_6(out_3[5]),
    .out_7(out_3[6]), .out_8(out_3[7]));
  SBox4Bit_F sbox4bit_f_3 (
    .in_1(in_1[8]), .in_2(in_1[9]), .in_3(in_1[10]), .in_4(in_1[11]), .out_5(out_3[8]), .out_6(out_3[9]),
    .out_7(out_3[10]), .out_8(out_3[11]));
  SBox4Bit_F sbox4bit_f_4 (
    .in_1(in_1[12]), .in_2(in_1[13]), .in_3(in_1[14]), .in_4(in_1[15]), .out_5(out_3[12]), .out_6(out_3[13]),
    .out_7(out_3[14]), .out_8(out_3[15]));
  SBox4Bit_F sbox4bit_f_5 (
    .in_1(in_1[16]), .in_2(in_1[17]), .in_3(in_1[18]), .in_4(in_1[19]), .out_5(out_3[16]), .out_6(out_3[17]),
    .out_7(out_3[18]), .out_8(out_3[19]));
  SBox4Bit_F sbox4bit_f_6 (
    .in_1(in_1[20]), .in_2(in_1[21]), .in_3(in_1[22]), .in_4(in_1[23]), .out_5(out_3[20]), .out_6(out_3[21]),
    .out_7(out_3[22]), .out_8(out_3[23]));
  SBox4Bit_F sbox4bit_f_7 (
    .in_1(in_1[24]), .in_2(in_1[25]), .in_3(in_1[26]), .in_4(in_1[27]), .out_5(out_3[24]), .out_6(out_3[25]),
    .out_7(out_3[26]), .out_8(out_3[27]));
  SBox4Bit_F sbox4bit_f_8 (
    .in_1(in_1[28]), .in_2(in_1[29]), .in_3(in_1[30]), .in_4(in_1[31]), .out_5(out_3[28]), .out_6(out_3[29]),
    .out_7(out_3[30]), .out_8(out_3[31]));
  SBox4Bit_F sbox4bit_f_9 (
    .in_1(in_2[0]), .in_2(in_2[1]), .in_3(in_2[2]), .in_4(in_2[3]), .out_5(out_4[0]), .out_6(out_4[1]),
    .out_7(out_4[2]), .out_8(out_4[3]));
  SBox4Bit_F sbox4bit_f_10 (
    .in_1(in_2[4]), .in_2(in_2[5]), .in_3(in_2[6]), .in_4(in_2[7]), .out_5(out_4[4]), .out_6(out_4[5]),
    .out_7(out_4[6]), .out_8(out_4[7]));
  SBox4Bit_F sbox4bit_f_11 (
    .in_1(in_2[8]), .in_2(in_2[9]), .in_3(in_2[10]), .in_4(in_2[11]), .out_5(out_4[8]), .out_6(out_4[9]),
    .out_7(out_4[10]), .out_8(out_4[11]));
  SBox4Bit_F sbox4bit_f_12 (
    .in_1(in_2[12]), .in_2(in_2[13]), .in_3(in_2[14]), .in_4(in_2[15]), .out_5(out_4[12]), .out_6(out_4[13]),
    .out_7(out_4[14]), .out_8(out_4[15]));
  SBox4Bit_F sbox4bit_f_13 (
    .in_1(in_2[16]), .in_2(in_2[17]), .in_3(in_2[18]), .in_4(in_2[19]), .out_5(out_4[16]), .out_6(out_4[17]),
    .out_7(out_4[18]), .out_8(out_4[19]));
  SBox4Bit_F sbox4bit_f_14 (
    .in_1(in_2[20]), .in_2(in_2[21]), .in_3(in_2[22]), .in_4(in_2[23]), .out_5(out_4[20]), .out_6(out_4[21]),
    .out_7(out_4[22]), .out_8(out_4[23]));
  SBox4Bit_F sbox4bit_f_15 (
    .in_1(in_2[24]), .in_2(in_2[25]), .in_3(in_2[26]), .in_4(in_2[27]), .out_5(out_4[24]), .out_6(out_4[25]),
    .out_7(out_4[26]), .out_8(out_4[27]));
  SBox4Bit_F sbox4bit_f_16 (
    .in_1(in_2[28]), .in_2(in_2[29]), .in_3(in_2[30]), .in_4(in_2[31]), .out_5(out_4[28]), .out_6(out_4[29]),
    .out_7(out_4[30]), .out_8(out_4[31]));
endmodule

module SPRLayer_F (
  input  [31:0] Key,
  input  [31:0] Key_2,
  input  [31:0] Cipher,
  input  [31:0] Cipher_2,
  output [31:0] Output,
  output [31:0] Output_2
);

  wire [31:0] pbox_f_1_out_3, pbox_f_1_out_4, sbox64bit_f_1_out_3, sbox64bit_f_1_out_4;

  SBox64Bit_F sbox64bit_f_1 (.in_1(Cipher), .in_2(Cipher_2), .out_3(sbox64bit_f_1_out_3), .out_4(sbox64bit_f_1_out_4));
  PBox_F pbox_f_1 (
    .in_1(sbox64bit_f_1_out_3), .in_2(sbox64bit_f_1_out_4), .out_3(pbox_f_1_out_3), .out_4(pbox_f_1_out_4));
  AddRoundKey_F addroundkey_f_1 (
    .in_1(Key), .in_2(Key_2), .in_3(pbox_f_1_out_3), .in_4(pbox_f_1_out_4), .out_5(Output), .out_6(Output_2));
endmodule

module KeyTransform_F (
  input  [15:0] in_1,
  input  [31:0] in_2,
  input  [31:0] in_3,
  output [15:0] out_4,
  output [31:0] out_5,
  output [31:0] out_6
);


  assign out_4 = in_1;
  assign out_5 = in_2;
  assign out_6 = in_3;
endmodule
