// Logisim project Test.circ as structural Verilog: 20 circuits, main circuit 4 bit Main
module _4_bit_Main (
  input  [3:0] in_1,
  input  _0,
  input  _1,
  input  _2,
  input  _3,
  input  _4,
  input  _5,
  input  _6,
  input  _7,
  input  _8,
  input  _9,
  input  A,
  input  B,
  input  C,
  input  D,
  input  E,
  input  F,
  input  _0_2,
  input  _1_2,
  input  _2_2,
  input  _3_2,
  input  _4_2,
  input  _5_2,
  input  _6_2,
  input  _7_2,
  input  _8_2,
  input  _9_2,
  input  A_2,
  input  B_2,
  input  C_2,
  input  D_2,
  input  E_2,
  input  F_2,
  input  _0_3,
  input  _1_3,
  input  _2_3,
  input  _3_3,
  input  _4_3,
  input  _5_3,
  input  _6_3,
  input  _7_3,
  input  _8_3,
  input  _9_3,
  input  A_3,
  input  B_3,
  input  C_3,
  input  D_3,
  input  E_3,
  input  F_3,
  input  _0_4,
  input  _1_4,
  input  _2_4,
  input  _3_4,
  input  _4_4,
  input  _5_4,
  input  _6_4,
  input  _7_4,
  input  _8_4,
  input  _9_4,
  input  A_4,
  input  B_4,
  input  C_4,
  input  D_4,
  input  E_4,
  input  F_4,
  output _0_5,
  output _1_5,
  output _2_5,
  output _3_5,
  output _4_5,
  output _5_5,
  output _6_5,
  output _7_5,
  output _8_5,
  output _9_5,
  output A_5,
  output B_5,
  output C_5,
  output D_5,
  output E_5,
  output F_5,
  output _0_6,
  output _1_6,
  output _2_6,
  output _3_6,
  output _4_6,
  output _5_6,
  output _6_6,
  output _7_6,
  output _8_6,
  output _9_6,
  output A_6,
  output B_6,
  output C_6,
  output D_6,
  output E_6,
  output F_6,
  output _0_7,
  output _1_7,
  output _2_7,
  output _3_7,
  output _4_7,
  output _5_7,
  output _6_7,
  output _7_7,
  output _8_7,
  output _9_7,
  output A_7,
  output B_7,
  output C_7,
  output D_7,
  output E_7,
  output F_7,
  output _0_8,
  output _1_8,
  output _2_8,
  output _3_8,
  output _4_8,
  output _5_8,
  output _6_8,
  output _7_8,
  output _8_8,
  output _9_8,
  output A_8,
  output B_8,
  output C_8,
  output D_8,
  output E_8,
  output F_8
);

  wire clock_1_out, clock_2_out, encoding_1_out_20, encoding_1_out_21, encoding_1_out_22, encoding_1_out_23,
       encoding_1_out_24, encoding_1_out_25, encoding_1_out_26, encoding_1_out_27, encoding_2_out_20,
       encoding_2_out_21, encoding_2_out_22, encoding_2_out_23, encoding_2_out_24, encoding_2_out_25,
       encoding_2_out_26, encoding_2_out_27, encoding_3_out_20, encoding_3_out_21, encoding_3_out_22,
       encoding_3_out_23, encoding_3_out_24, encoding_3_out_25, encoding_3_out_26, encoding_3_out_27,
       encoding_4_out_20, encoding_4_out_21, encoding_4_out_22, encoding_4_out_23, encoding_4_out_24,
       encoding_4_out_25, encoding_4_out_26, encoding_4_out_27;

  Clock clock_1 (.out(clock_1_out));
  Clock clock_2 (.out(clock_2_out));
  encoding encoding_1 (
    .Public_Key(in_1), ._0(_0), ._1(_1), ._2(_2), ._3(_3), ._4(_4), ._5(_5), ._6(_6), ._7(_7), ._8(_8),
    ._9(_9), .A(A), .B(B), .C(C), .D(D), .E(E), .F(F), .Main_Clock(clock_1_out),
    .Register_clock(clock_2_out), .out_20(encoding_1_out_20), .out_21(encoding_1_out_21),
    .out_22(encoding_1_out_22), .out_23(encoding_1_out_23), .out_24(encoding_1_out_24),
    .out_25(encoding_1_out_25), .out_26(encoding_1_out_26), .out_27(encoding_1_out_27));
  encoding encoding_2 (
    .Public_Key(in_1), ._0(_0_2), ._1(_1_2), ._2(_2_2), ._3(_3_2), ._4(_4_2), ._5(_5_2), ._6(_6_2),
    ._7(_7_2), ._8(_8_2), ._9(_9_2), .A(A_2), .B(B_2), .C(C_2), .D(D_2), .E(E_2), .F(F_2),
    .Main_Clock(clock_1_out), .Register_clock(clock_2_out), .out_20(encoding_2_out_20),
    .out_21(encoding_2_out_21), .out_22(encoding_2_out_22), .out_23(encoding_2_out_23),
    .out_24(encoding_2_out_24), .out_25(encoding_2_out_25), .out_26(encoding_2_out_26),
    .out_27(encoding_2_out_27));
  encoding encoding_3 (
    .Public_Key(in_1), ._0(_0_3), ._1(_1_3), ._2(_2_3), ._3(_3_3), ._4(_4_3), ._5(_5_3), ._6(_6_3),
    ._7(_7_3), ._8(_8_3), ._9(_9_3), .A(A_3), .B(B_3), .C(C_3), .D(D_3), .E(E_3), .F(F_3),
    .Main_Clock(clock_1_out), .Register_clock(clock_2_out), .out_20(encoding_3_out_20),
    .out_21(encoding_3_out_21), .out_22(encoding_3_out_22), .out_23(encoding_3_out_23),
    .out_24(encoding_3_out_24), .out_25(encoding_3_out_25), .out_26(encoding_3_out_26),
    .out_27(encoding_3_out_27));
  encoding encoding_4 (
    .Public_Key(in_1), ._0(_0_4), ._1(_1_4), ._2(_2_4), ._3(_3_4), ._4(_4_4), ._5(_5_4), ._6(_6_4),
    ._7(_7_4), ._8(_8_4), ._9(_9_4), .A(A_4), .B(B_4), .C(C_4), .D(D_4), .E(E_4), .F(F_4),
    .Main_Clock(clock_1_out), .Register_clock(clock_2_out), .out_20(encoding_4_out_20),
    .out_21(encoding_4_out_21), .out_22(encoding_4_out_22), .out_23(encoding_4_out_23),
    .out_24(encoding_4_out_24), .out_25(encoding_4_out_25), .out_26(encoding_4_out_26),
    .out_27(encoding_4_out_27));
  decoding decoding_1 (
    .Private_Key(encoding_1_out_20), .in_2(encoding_1_out_21), .in_3(encoding_1_out_22),
    .in_4(encoding_1_out_23), .clock(clock_1_out), .in_6(in_1), .clock_2(clock_1_out),
    .encrypted(encoding_1_out_24), .data(encoding_1_out_25), .in_10(encoding_1_out_26),
    .in_11(encoding_1_out_27), ._0(_0_5), ._1(_1_5), ._2(_2_5), ._3(_3_5), ._4(_4_5), ._5(_5_5), ._6(_6_5),
    ._7(_7_5), ._8(_8_5), ._9(_9_5), .A(A_5), .B(B_5), .C(C_5), .D(D_5), .E(E_5), .F(F_5));
  decoding decoding_2 (
    .Private_Key(encoding_2_out_20), .in_2(encoding_2_out_21), .in_3(encoding_2_out_22),
    .in_4(encoding_2_out_23), .clock(clock_1_out), .in_6(in_1), .clock_2(clock_1_out),
    .encrypted(encoding_2_out_24), .data(encoding_2_out_25), .in_10(encoding_2_out_26),
    .in_11(encoding_2_out_27), ._0(_0_6), ._1(_1_6), ._2(_2_6), ._3(_3_6), ._4(_4_6), ._5(_5_6), ._6(_6_6),
    ._7(_7_6), ._8(_8_6), ._9(_9_6), .A(A_6), .B(B_6), .C(C_6), .D(D_6), .E(E_6), .F(F_6));
  decoding decoding_3 (
    .Private_Key(encoding_3_out_20), .in_2(encoding_3_out_21), .in_3(encoding_3_out_22),
    .in_4(encoding_3_out_23), .clock(clock_1_out), .in_6(in_1), .clock_2(clock_1_out),
    .encrypted(encoding_3_out_24), .data(encoding_3_out_25), .in_10(encoding_3_out_26),
    .in_11(encoding_3_out_27), ._0(_0_7), ._1(_1_7), ._2(_2_7), ._3(_3_7), ._4(_4_7), ._5(_5_7), ._6(_6_7),
    ._7(_7_7), ._8(_8_7), ._9(_9_7), .A(A_7), .B(B_7), .C(C_7), .D(D_7), .E(E_7), .F(F_7));
  decoding decoding_4 (
    .Private_Key(encoding_4_out_20), .in_2(encoding_4_out_21), .in_3(encoding_4_out_22),
    .in_4(encoding_4_out_23), .clock(clock_1_out), .in_6(in_1), .clock_2(clock_1_out),
    .encrypted(encoding_4_out_24), .data(encoding_4_out_25), .in_10(encoding_4_out_26),
    .in_11(encoding_4_out_27), ._0(_0_8), ._1(_1_8), ._2(_2_8), ._3(_3_8), ._4(_4_8), ._5(_5_8), ._6(_6_8),
    ._7(_7_8), ._8(_8_8), ._9(_9_8), .A(A_8), .B(B_8), .C(C_8), .D(D_8), .E(E_8), .F(F_8));

  // Notes on the sheet:
  //   Public Key
  //   INPUT
  //   Main Clock
  //   Register Clock
  //   Encryption
  //   4 BIT MODEL OF ENCRYPTION- DECRYPTION
  //   Encryption
  //   Encryption
  //   Encryption
  //   ENCRYPTION AND DECRYPTION USING ASYMMETRIC KEY
  //   This is 4 bit Encryption Decryption Model in which Hexadecimal numbers are taken as input and which are then encrypted and then decrypted
  //   using public and private keys
  //   Decryption
  //   Decryption
  //   Decryption
  //   Decryption
  //   Shushant Kumar 16CO143
  //   Anmol Horo 16CO206
  //   OUTPUT
endmodule

module _1_bit_main (
  input  [3:0] PUBLIC_Key,
  input  _0,
  input  _1,
  input  _2,
  input  _3,
  input  _4,
  input  _5,
  input  _6,
  input  _7,
  input  _8,
  input  _9,
  input  A,
  input  B,
  input  C,
  input  D,
  input  E,
  input  F,
  output _0_2,
  output _1_2,
  output _2_2,
  output _3_2,
  output _4_2,
  output _5_2,
  output _6_2,
  output _7_2,
  output _8_2,
  output _9_2,
  output A_2,
  output B_2,
  output C_2,
  output D_2,
  output E_2,
  output F_2
);

  wire clock_1_out, clock_2_out, encoding_1_out_20, encoding_1_out_21, encoding_1_out_22, encoding_1_out_23,
       encoding_1_out_24, encoding_1_out_25, encoding_1_out_26, encoding_1_out_27;

  Clock clock_1 (.out(clock_1_out));
  Clock clock_2 (.out(clock_2_out));
  encoding encoding_1 (
    .Public_Key(PUBLIC_Key), ._0(_0), ._1(_1), ._2(_2), ._3(_3), ._4(_4), ._5(_5), ._6(_6), ._7(_7), ._8(_8),
    ._9(_9), .A(A), .B(B), .C(C), .D(D), .E(E), .F(F), .Main_Clock(clock_1_out),
    .Register_clock(clock_2_out), .out_20(encoding_1_out_20), .out_21(encoding_1_out_21),
    .out_22(encoding_1_out_22), .out_23(encoding_1_out_23), .out_24(encoding_1_out_24),
    .out_25(encoding_1_out_25), .out_26(encoding_1_out_26), .out_27(encoding_1_out_27));
  decoding decoding_1 (
    .Private_Key(encoding_1_out_20), .in_2(encoding_1_out_21), .in_3(encoding_1_out_22),
    .in_4(encoding_1_out_23), .clock(clock_1_out), .in_6(PUBLIC_Key), .clock_2(clock_1_out),
    .encrypted(encoding_1_out_24), .data(encoding_1_out_25), .in_10(encoding_1_out_26),
    .in_11(encoding_1_out_27), ._0(_0_2), ._1(_1_2), ._2(_2_2), ._3(_3_2), ._4(_4_2), ._5(_5_2), ._6(_6_2),
    ._7(_7_2), ._8(_8_2), ._9(_9_2), .A(A_2), .B(B_2), .C(C_2), .D(D_2), .E(E_2), .F(F_2));

  // Notes on the sheet:
  //   Main Clock
  //   Register Clock
  //   Encryption
  //   1 BIT MODEL OF ENCRYPTION- DECRYPTION
  //   using public and private keys
  //   This is 1bit Encryption Decryption Model in which Hexadecimal numbers are taken as input and which are then encrypted and then decrypted
  //   DECRYPTION
endmodule

module encoding (
  input  [3:0] Public_Key,
  input  _0,
  input  _1,
  input  _2,
  input  _3,
  input  _4,
  input  _5,
  input  _6,
  input  _7,
  input  _8,
  input  _9,
  input  A,
  input  B,
  input  C,
  input  D,
  input  E,
  input  F,
  input  Main_Clock,
  input  Register_clock,
  output out_20,
  output out_21,
  output out_22,
  output out_23,
  output out_24,
  output out_25,
  output out_26,
  output out_27
);

  wire binary_to_grey_1_out_5, binary_to_grey_1_out_6, binary_to_grey_1_out_7, binary_to_grey_1_out_8,
       encoder_1_w, encoder_1_x, encoder_1_y, encoder_1_z, justxor_1_out_9, justxor_1_out_10,
       justxor_1_out_11, justxor_1_out_12, negation_1_a_prime, negation_1_b_prime, negation_1_c_prime,
       negation_1_d_prime, private_key_generate_1_a_b_c_d, private_key_generate_1_out_6,
       private_key_generate_1_out_7, private_key_generate_1_out_8;

  negation negation_1 (
    .A(encoder_1_z), .B(encoder_1_y), .C(encoder_1_x), .D(encoder_1_w), .A_prime(negation_1_a_prime),
    .B_prime(negation_1_b_prime), .C_prime(negation_1_c_prime), .D_prime(negation_1_d_prime));
  encoder encoder_1 (
    ._0(_0), ._1(_1), ._2(_2), ._3(_3), ._4(_4), ._5(_5), ._6(_6), ._7(_7), ._8(_8), ._9(_9), .A(A), .B(B),
    .C(C), .D(D), .E(E), .F(F), .Z(encoder_1_z), .Y(encoder_1_y), .X(encoder_1_x), .W(encoder_1_w));
  binary_to_grey binary_to_grey_1 (
    .A(negation_1_a_prime), .B(negation_1_b_prime), .C(negation_1_c_prime), .D(negation_1_d_prime),
    .out_5(binary_to_grey_1_out_5), .out_6(binary_to_grey_1_out_6), .out_7(binary_to_grey_1_out_7),
    .out_8(binary_to_grey_1_out_8));
  private_key_generate private_key_generate_1 (
    .A(binary_to_grey_1_out_5), .B(binary_to_grey_1_out_6), .C(binary_to_grey_1_out_7),
    .D(binary_to_grey_1_out_8), .A_B_C_D(private_key_generate_1_a_b_c_d),
    .out_6(private_key_generate_1_out_6), .out_7(private_key_generate_1_out_7),
    .out_8(private_key_generate_1_out_8));
  public_XOR public_xor_1 (
    .in_1(Public_Key), .Clock(Main_Clock), .A(justxor_1_out_9), .B(justxor_1_out_10), .C(justxor_1_out_11),
    .D(justxor_1_out_12), .A_XOR_P_0(out_24), .B_XOR_P_1(out_25), .C_XOR_P_2(out_26), .D_XOR_P_3(out_27));
  justxor justxor_1 (
    .in_1(binary_to_grey_1_out_5), .A(private_key_generate_1_a_b_c_d), .in_3(binary_to_grey_1_out_6),
    .B(private_key_generate_1_out_6), .in_5(binary_to_grey_1_out_7), .C(private_key_generate_1_out_7),
    .in_7(binary_to_grey_1_out_8), .D(private_key_generate_1_out_8), .out_9(justxor_1_out_9),
    .out_10(justxor_1_out_10), .out_11(justxor_1_out_11), .out_12(justxor_1_out_12));
  _4bit_reg u_4bit_reg_1 (
    .A0(private_key_generate_1_a_b_c_d), .A1(private_key_generate_1_out_6),
    .A2(private_key_generate_1_out_7), .A3(private_key_generate_1_out_8), .Clock(Register_clock),
    .A0_2(out_20), .A1_2(out_21), .A2_2(out_22), .A3_2(out_23));

  // Notes on the sheet:
  //   negation
  //   binary
  //   to
  //   grey code
  //   16:4 encoder
  //   Complete Encryption Block
  //   private key
  //   generator
  //   This block represents the all the steps in encryption process
  //   XOR with
  //   Private key
  //   XOR with
  //   Public key
  //   4bit Register
  //   Encrypted data
  //   Private Keys generated
endmodule

module encoder (
  input  _0,
  input  _1,
  input  _2,
  input  _3,
  input  _4,
  input  _5,
  input  _6,
  input  _7,
  input  _8,
  input  _9,
  input  A,
  input  B,
  input  C,
  input  D,
  input  E,
  input  F,
  output Z,
  output Y,
  output X,
  output W
);

  or or_1 (Z, _1, _3, _5, _7, _9, B, D, F);
  or or_2 (Y, _2, _3, _6, _7, A, B, E, F);
  or or_3 (X, _4, _5, _6, _7, C, D, E, F);
  or or_4 (W, _8, A, B, C, D, E, _9, F);

  // Notes on the sheet:
  //   16:4  Encoder
  //   Hexadecimal inputs are taken and converted to their binary equivalent in the following manner
endmodule

module negation (
  input  A,
  input  B,
  input  C,
  input  D,
  output A_prime,
  output B_prime,
  output C_prime,
  output D_prime
);

  xor xor_1 (A_prime, 1'b1, A);
  xor xor_2 (B_prime, 1'b1, B);
  xor xor_3 (C_prime, 1'b1, C);
  xor xor_4 (D_prime, 1'b1, D);

  // Notes on the sheet:
  //   Negation Model
  //   This model takes 4bit input and returns there complement using only XOR gates
endmodule

module binary_to_grey (
  input  A,
  input  B,
  input  C,
  input  D,
  output out_5,
  output out_6,
  output out_7,
  output out_8
);

  xor xor_1 (out_6, A, B);
  xor xor_2 (out_7, B, C);
  xor xor_3 (out_8, C, D);

  assign out_5 = A;

  // Notes on the sheet:
  //   Binary to Grey Code
  //   4 bit Binary inputs are taken and converted to grey code in the following manner
endmodule

module private_key_generate (
  input  A,
  input  B,
  input  C,
  input  D,
  output A_B_C_D,
  output out_6,
  output out_7,
  output out_8
);

  wire and_1_out, and_2_out, and_3_out, and_4_out, and_5_out, and_6_out, and_7_out, and_8_out, and_9_out,
       and_10_out;

  and and_1 (and_1_out, D, C);
  and and_2 (and_2_out, D, B);
  and and_3 (and_3_out, C, A);
  and and_4 (and_4_out, C, B);
  and and_5 (and_5_out, B, A);
  and and_6 (and_6_out, A, B, C);
  and and_7 (and_7_out, B, C, D);
  and and_8 (and_8_out, D, A);
  and and_9 (and_9_out, D, A, B);
  and and_10 (and_10_out, C, D, A);
  and and_11 (A_B_C_D, A, B, C, D);
  or or_1 (out_8, D, A, B, C);
  or or_2 (out_6, and_6_out, and_9_out, and_7_out, and_10_out);
  or or_3 (out_7, and_1_out, and_2_out, and_3_out, and_8_out, and_4_out, and_5_out);

  // Notes on the sheet:
  //   Generating Unique Private Key 
  //   With the given 4-1bit input A,B,C,D we are generating a unique key
  //   The 4 output are the operations on the input 4bits as shown above
  //   A.B.C+B.C.D+A.C.D+A.B.D
  //   A.B+B.C+C.D+A.C+A.D+B.D
  //   A+B+C+D
endmodule

module DFF (
  input  D,
  input  Clock,
  output Q,
  output Q_prime
);

  wire nand_1_out, nand_2_out, nand_3_out;

  nand nand_1 (nand_1_out, D, D);
  nand nand_2 (nand_2_out, Clock, D);
  nand nand_3 (nand_3_out, nand_1_out, Clock);
  nand nand_4 (Q, Clock, nand_2_out, Q_prime);
  nand nand_5 (Q_prime, Q, nand_3_out, Clock);

  // Notes on the sheet:
  //   Implemented D Flip Flop
  //   D Flip Flop
endmodule

module _4bit_reg (
  input  A0,
  input  A1,
  input  A2,
  input  A3,
  input  Clock,
  output A0_2,
  output A1_2,
  output A2_2,
  output A3_2
);

  DFF dff_1 (.D(A3), .Clock(Clock), .Q(A3_2));  // open: Q_prime
  DFF dff_2 (.D(A2), .Clock(Clock), .Q(A2_2));  // open: Q_prime
  DFF dff_3 (.D(A1), .Clock(Clock), .Q(A1_2));  // open: Q_prime
  DFF dff_4 (.D(A0), .Clock(Clock), .Q(A0_2));  // open: Q_prime

  // Notes on the sheet:
  //   4 Bit Register
  //   This block stores 4 bit Input
endmodule

module justxor (
  input  in_1,
  input  A,
  input  in_3,
  input  B,
  input  in_5,
  input  C,
  input  in_7,
  input  D,
  output out_9,
  output out_10,
  output out_11,
  output out_12
);

  xor xor_1 (out_9, in_1, A);
  xor xor_2 (out_10, in_3, B);
  xor xor_3 (out_11, in_5, C);
  xor xor_4 (out_12, in_7, D);

  // Notes on the sheet:
  //   XOR function
  //   Inputs are taken and are XOR with each other in the following manner
endmodule

module public_XOR (
  input  [3:0] in_1,
  input  Clock,
  input  A,
  input  B,
  input  C,
  input  D,
  output A_XOR_P_0,
  output B_XOR_P_1,
  output C_XOR_P_2,
  output D_XOR_P_3
);

  wire [3:0] register_1_q;

  Register #(.width(4)) register_1 (.D(in_1), .en(1'b1), .Q(register_1_q), .clk(Clock), .clr(1'b0));
  xor xor_1 (A_XOR_P_0, register_1_q[0], A);
  xor xor_2 (B_XOR_P_1, register_1_q[1], B);
  xor xor_3 (C_XOR_P_2, register_1_q[2], C);
  xor xor_4 (D_XOR_P_3, register_1_q[3], D);

  // Notes on the sheet:
  //   PUBLIC Key P[3:0]
  //   XOR with PUBLIC KEY
  //   In this model we have implemented a block which XOR the input with the public key stored in a register
endmodule

module decoding (
  input  Private_Key,
  input  in_2,
  input  in_3,
  input  in_4,
  input  clock,
  input  [3:0] in_6,
  input  clock_2,
  input  encrypted,
  input  data,
  input  in_10,
  input  in_11,
  output _0,
  output _1,
  output _2,
  output _3,
  output _4,
  output _5,
  output _6,
  output _7,
  output _8,
  output _9,
  output A,
  output B,
  output C,
  output D,
  output E,
  output F
);

  wire grey_to_binary_1_w, grey_to_binary_1_x, grey_to_binary_1_y, grey_to_binary_1_z, negate_1_out_5,
       negate_1_out_6, negate_1_out_7, negate_1_out_8, public_xor_1_a_xor_p_0, public_xor_1_b_xor_p_1,
       public_xor_1_c_xor_p_2, public_xor_1_d_xor_p_3, public_xor_2_a_xor_p_0, public_xor_2_b_xor_p_1,
       public_xor_2_c_xor_p_2, public_xor_2_d_xor_p_3;

  public_xor public_xor_1 (
    .in_1(in_6), .Clock(clock_2), .A(encrypted), .B(data), .C(in_10), .D(in_11),
    .A_XOR_P_0(public_xor_1_a_xor_p_0), .B_XOR_P_1(public_xor_1_b_xor_p_1),
    .C_XOR_P_2(public_xor_1_c_xor_p_2), .D_XOR_P_3(public_xor_1_d_xor_p_3));
  public_xor public_xor_2 (
    .in_1({in_4, in_3, in_2, Private_Key}), .Clock(clock), .A(public_xor_1_a_xor_p_0),
    .B(public_xor_1_b_xor_p_1), .C(public_xor_1_c_xor_p_2), .D(public_xor_1_d_xor_p_3),
    .A_XOR_P_0(public_xor_2_a_xor_p_0), .B_XOR_P_1(public_xor_2_b_xor_p_1),
    .C_XOR_P_2(public_xor_2_c_xor_p_2), .D_XOR_P_3(public_xor_2_d_xor_p_3));
  grey_to_binary grey_to_binary_1 (
    .A(public_xor_2_a_xor_p_0), .B(public_xor_2_b_xor_p_1), .C(public_xor_2_c_xor_p_2),
    .D(public_xor_2_d_xor_p_3), .W(grey_to_binary_1_w), .X(grey_to_binary_1_x), .Y(grey_to_binary_1_y),
    .Z(grey_to_binary_1_z));
  negate negate_1 (
    .in_1(grey_to_binary_1_w), .in_2(grey_to_binary_1_x), .in_3(grey_to_binary_1_y),
    .in_4(grey_to_binary_1_z), .out_5(negate_1_out_5), .out_6(negate_1_out_6), .out_7(negate_1_out_7),
    .out_8(negate_1_out_8));
  decoder decoder_1 (
    .W(negate_1_out_8), .X(negate_1_out_7), .Y(negate_1_out_6), .Z(negate_1_out_5), ._0(_0), ._1(_1),
    ._2(_2), ._3(_3), ._4(_4), ._5(_5), ._6(_6), ._7(_7), ._8(_8), ._9(_9), .A(A), .B(B), .C(C), .D(D),
    .E(E), .F(F));

  // Notes on the sheet:
  //   Public Key
  //   XOR with
  //   Public Key
  //   XOR with private key
  //   Complete Decryption Block
  //   This block represents the all the steps in decryption process
  //   grey code 
  //   to
  //   Binary
  //   negation
  //   16:4 decoder
endmodule

module public_xor (
  input  [3:0] in_1,
  input  Clock,
  input  A,
  input  B,
  input  C,
  input  D,
  output A_XOR_P_0,
  output B_XOR_P_1,
  output C_XOR_P_2,
  output D_XOR_P_3
);

  wire [3:0] register_1_q;

  Register #(.width(4)) register_1 (.D(in_1), .en(1'b1), .Q(register_1_q), .clk(Clock), .clr(1'b0));
  xor xor_1 (A_XOR_P_0, register_1_q[0], A);
  xor xor_2 (B_XOR_P_1, register_1_q[1], B);
  xor xor_3 (C_XOR_P_2, register_1_q[2], C);
  xor xor_4 (D_XOR_P_3, register_1_q[3], D);

  // Notes on the sheet:
  //   PUBLIC Key P[3:0]
  //   XOR with PUBLIC KEY
  //   In this model we have implemented a block which XOR the input with the public key stored in a register
endmodule

module grey_to_binary (
  input  A,
  input  B,
  input  C,
  input  D,
  output W,
  output X,
  output Y,
  output Z
);

  xor xor_1 (X, A, B);
  xor xor_2 (Y, X, C);
  xor xor_3 (Z, Y, D);

  assign W = A;

  // Notes on the sheet:
  //   Grey code to binary
  //   Grey code inputs are taken and converted into its binary equivalent in the following manner
endmodule

module negate (
  input  in_1,
  input  in_2,
  input  in_3,
  input  in_4,
  output out_5,
  output out_6,
  output out_7,
  output out_8
);

  xor xor_1 (out_5, 1'b1, in_1);
  xor xor_2 (out_6, 1'b1, in_2);
  xor xor_3 (out_7, in_3, 1'b1);
  xor xor_4 (out_8, 1'b1, in_4);

  // Notes on the sheet:
  //   Negation Model
  //   This model takes 4bit input and returns there complement using only XOR gates
endmodule

module decoder (
  input  W,
  input  X,
  input  Y,
  input  Z,
  output _0,
  output _1,
  output _2,
  output _3,
  output _4,
  output _5,
  output _6,
  output _7,
  output _8,
  output _9,
  output A,
  output B,
  output C,
  output D,
  output E,
  output F
);

  wire not_1_out, not_2_out, not_3_out, not_4_out;

  not not_1 (not_1_out, W);
  not not_2 (not_2_out, Y);
  not not_3 (not_3_out, X);
  not not_4 (not_4_out, Z);
  and and_1 (_0, not_4_out, not_2_out, not_3_out, not_1_out);
  and and_2 (_1, Z, not_2_out, not_3_out, not_1_out);
  and and_3 (_2, Y, not_4_out, not_1_out, not_3_out);
  and and_4 (_3, Z, Y, not_1_out, not_3_out);
  and and_5 (_4, not_4_out, not_2_out, X, not_1_out);
  and and_6 (_5, Z, not_2_out, X, not_1_out);
  and and_7 (_7, Z, Y, X, not_1_out);
  and and_8 (_8, W, not_4_out, not_2_out, not_3_out);
  and and_9 (_9, W, Z, not_2_out, not_3_out);
  and and_10 (A, not_4_out, Y, not_3_out, W);
  and and_11 (B, Z, Y, not_3_out, W);
  and and_12 (C, not_4_out, not_2_out, X, W);
  and and_13 (D, W, X, not_2_out, Z);
  and and_14 (E, W, X, Y, not_4_out);
  and and_15 (F, W, X, Y, Z);
  and and_16 (_6, not_1_out, X, Y, not_4_out);

  // Notes on the sheet:
  //   4:16 Decoder
  //   4 bit binary number is converted to hexadecimal numbers.
endmodule

module _4bit_Encryption (
  input  [3:0] Public_Key,
  input  _0,
  input  _1,
  input  _2,
  input  _3,
  input  _4,
  input  _5,
  input  _6,
  input  _7,
  input  _8,
  input  _9,
  input  A,
  input  B,
  input  C,
  input  D,
  input  E,
  input  F,
  input  _0_2,
  input  _1_2,
  input  _2_2,
  input  _3_2,
  input  _4_2,
  input  _5_2,
  input  _6_2,
  input  _7_2,
  input  _8_2,
  input  _9_2,
  input  A_2,
  input  B_2,
  input  C_2,
  input  D_2,
  input  E_2,
  input  F_2,
  input  _0_3,
  input  _1_3,
  input  _2_3,
  input  _3_3,
  input  _4_3,
  input  _5_3,
  input  _6_3,
  input  _7_3,
  input  _8_3,
  input  _9_3,
  input  A_3,
  input  B_3,
  input  C_3,
  input  D_3,
  input  E_3,
  input  F_3,
  input  _0_4,
  input  _1_4,
  input  _2_4,
  input  _3_4,
  input  _4_4,
  input  _5_4,
  input  _6_4,
  input  _7_4,
  input  _8_4,
  input  _9_4,
  input  A_4,
  input  B_4,
  input  C_4,
  input  D_4,
  input  E_4,
  input  F_4,
  output out_66,
  output out_67,
  output out_68,
  output out_69,
  output out_70,
  output out_71,
  output out_72,
  output out_73,
  output out_74,
  output out_75,
  output out_76,
  output out_77,
  output out_78,
  output out_79,
  output out_80,
  output out_81,
  output out_82,
  output out_83,
  output out_84,
  output out_85,
  output out_86,
  output out_87,
  output out_88,
  output out_89,
  output out_90,
  output out_91,
  output out_92,
  output out_93,
  output out_94,
  output out_95,
  output out_96,
  output out_97
);

  wire clock_1_out, clock_2_out;

  Clock clock_1 (.out(clock_1_out));
  Clock clock_2 (.out(clock_2_out));
  encoding encoding_1 (
    .Public_Key(Public_Key), ._0(_0), ._1(_1), ._2(_2), ._3(_3), ._4(_4), ._5(_5), ._6(_6), ._7(_7), ._8(_8),
    ._9(_9), .A(A), .B(B), .C(C), .D(D), .E(E), .F(F), .Main_Clock(clock_1_out),
    .Register_clock(clock_2_out), .out_20(out_66), .out_21(out_67), .out_22(out_68), .out_23(out_69),
    .out_24(out_70), .out_25(out_71), .out_26(out_72), .out_27(out_73));
  encoding encoding_2 (
    .Public_Key(Public_Key), ._0(_0_2), ._1(_1_2), ._2(_2_2), ._3(_3_2), ._4(_4_2), ._5(_5_2), ._6(_6_2),
    ._7(_7_2), ._8(_8_2), ._9(_9_2), .A(A_2), .B(B_2), .C(C_2), .D(D_2), .E(E_2), .F(F_2),
    .Main_Clock(clock_1_out), .Register_clock(clock_2_out), .out_20(out_74), .out_21(out_75),
    .out_22(out_76), .out_23(out_77), .out_24(out_78), .out_25(out_79), .out_26(out_80), .out_27(out_81));
  encoding encoding_3 (
    .Public_Key(Public_Key), ._0(_0_3), ._1(_1_3), ._2(_2_3), ._3(_3_3), ._4(_4_3), ._5(_5_3), ._6(_6_3),
    ._7(_7_3), ._8(_8_3), ._9(_9_3), .A(A_3), .B(B_3), .C(C_3), .D(D_3), .E(E_3), .F(F_3),
    .Main_Clock(clock_1_out), .Register_clock(clock_2_out), .out_20(out_82), .out_21(out_83),
    .out_22(out_84), .out_23(out_85), .out_24(out_86), .out_25(out_87), .out_26(out_88), .out_27(out_89));
  encoding encoding_4 (
    .Public_Key(Public_Key), ._0(_0_4), ._1(_1_4), ._2(_2_4), ._3(_3_4), ._4(_4_4), ._5(_5_4), ._6(_6_4),
    ._7(_7_4), ._8(_8_4), ._9(_9_4), .A(A_4), .B(B_4), .C(C_4), .D(D_4), .E(E_4), .F(F_4),
    .Main_Clock(clock_1_out), .Register_clock(clock_2_out), .out_20(out_90), .out_21(out_91),
    .out_22(out_92), .out_23(out_93), .out_24(out_94), .out_25(out_95), .out_26(out_96), .out_27(out_97));

  // Notes on the sheet:
  //   Main Clock
  //   Register Clock
  //   Encryption
  //   Encryption
  //   Encryption
  //   Encryption
  //   4 bit encryption model
  //   4 bit hexadecimal numbers are accepted and then they are encrypted using public and private key 
  //   Encrypted data
  //   Encrypted data
  //   Encrypted data
  //   Encrypted data
  //   Private Keys generated
  //   Private Keys generated
  //   Private Keys generated
  //   Private Keys generated
endmodule

module encryption (
  input  [3:0] Public_Key,
  input  _0,
  input  _1,
  input  _2,
  input  _3,
  input  _4,
  input  _5,
  input  _6,
  input  _7,
  input  _8,
  input  _9,
  input  A,
  input  B,
  input  C,
  input  D,
  input  E,
  input  F,
  output out_18,
  output out_19,
  output out_20,
  output out_21,
  output out_22,
  output out_23,
  output Encrypted_data,
  output out_25
);

  wire clock_1_out, clock_2_out;

  Clock clock_1 (.out(clock_1_out));
  Clock clock_2 (.out(clock_2_out));
  encoding encoding_1 (
    .Public_Key(Public_Key), ._0(_0), ._1(_1), ._2(_2), ._3(_3), ._4(_4), ._5(_5), ._6(_6), ._7(_7), ._8(_8),
    ._9(_9), .A(A), .B(B), .C(C), .D(D), .E(E), .F(F), .Main_Clock(clock_1_out),
    .Register_clock(clock_2_out), .out_20(out_18), .out_21(out_19), .out_22(out_20), .out_23(out_21),
    .out_24(out_22), .out_25(out_23), .out_26(Encrypted_data), .out_27(out_25));

  // Notes on the sheet:
  //   Main Clock
  //   Register Clock
  //   Encryption
  //   1 bit encryption model
  //   1 bit hexadecimal numbers are accepted and then they are encrypted using public and private key 
  //   Private Keys 
  //   generated
endmodule

module _4_bit_decryption (
  input  [3:0] Public_Key,
  input  Private_Key,
  input  in_3,
  input  in_4,
  input  in_5,
  input  in_6,
  input  encrypted,
  input  in_8,
  input  in_9,
  input  in_10,
  input  Private_Key_2,
  input  in_12,
  input  in_13,
  input  in_14,
  input  encrypted_2,
  input  data,
  input  in_17,
  input  Private_Key_3,
  input  in_19,
  input  in_20,
  input  in_21,
  input  in_22,
  input  in_23,
  input  data_2,
  input  in_25,
  input  Private_Key_4,
  input  in_27,
  input  in_28,
  input  in_29,
  input  in_30,
  input  encrypted_3,
  input  data_3,
  input  in_33,
  output _0,
  output _1,
  output _2,
  output _3,
  output _4,
  output _5,
  output _6,
  output _7,
  output _8,
  output _9,
  output A,
  output B,
  output C,
  output D,
  output E,
  output F,
  output _0_2,
  output _1_2,
  output _2_2,
  output _3_2,
  output _4_2,
  output _5_2,
  output _6_2,
  output _7_2,
  output _8_2,
  output _9_2,
  output A_2,
  output B_2,
  output C_2,
  output D_2,
  output E_2,
  output F_2,
  output _0_3,
  output _1_3,
  output _2_3,
  output _3_3,
  output _4_3,
  output _5_3,
  output _6_3,
  output _7_3,
  output _8_3,
  output _9_3,
  output A_3,
  output B_3,
  output C_3,
  output D_3,
  output E_3,
  output F_3,
  output _0_4,
  output _1_4,
  output _2_4,
  output _3_4,
  output _4_4,
  output _5_4,
  output _6_4,
  output _7_4,
  output _8_4,
  output _9_4,
  output A_4,
  output B_4,
  output C_4,
  output D_4,
  output E_4,
  output F_4
);

  wire clock_1_out;

  Clock clock_1 (.out(clock_1_out));
  decoding decoding_1 (
    .Private_Key(Private_Key), .in_2(in_3), .in_3(in_4), .in_4(in_5), .clock(clock_1_out), .in_6(Public_Key),
    .clock_2(clock_1_out), .encrypted(in_6), .data(encrypted), .in_10(in_8), .in_11(in_9), ._0(_0), ._1(_1),
    ._2(_2), ._3(_3), ._4(_4), ._5(_5), ._6(_6), ._7(_7), ._8(_8), ._9(_9), .A(A), .B(B), .C(C), .D(D),
    .E(E), .F(F));
  decoding decoding_2 (
    .Private_Key(in_10), .in_2(Private_Key_2), .in_3(in_12), .in_4(in_13), .clock(clock_1_out),
    .in_6(Public_Key), .clock_2(clock_1_out), .encrypted(in_14), .data(encrypted_2), .in_10(data),
    .in_11(in_17), ._0(_0_2), ._1(_1_2), ._2(_2_2), ._3(_3_2), ._4(_4_2), ._5(_5_2), ._6(_6_2), ._7(_7_2),
    ._8(_8_2), ._9(_9_2), .A(A_2), .B(B_2), .C(C_2), .D(D_2), .E(E_2), .F(F_2));
  decoding decoding_3 (
    .Private_Key(Private_Key_3), .in_2(in_19), .in_3(in_20), .in_4(in_21), .clock(clock_1_out),
    .in_6(Public_Key), .clock_2(clock_1_out), .encrypted(in_22), .data(in_23), .in_10(data_2), .in_11(in_25),
    ._0(_0_3), ._1(_1_3), ._2(_2_3), ._3(_3_3), ._4(_4_3), ._5(_5_3), ._6(_6_3), ._7(_7_3), ._8(_8_3),
    ._9(_9_3), .A(A_3), .B(B_3), .C(C_3), .D(D_3), .E(E_3), .F(F_3));
  decoding decoding_4 (
    .Private_Key(Private_Key_4), .in_2(in_27), .in_3(in_28), .in_4(in_29), .clock(clock_1_out),
    .in_6(Public_Key), .clock_2(clock_1_out), .encrypted(in_30), .data(encrypted_3), .in_10(data_3),
    .in_11(in_33), ._0(_0_4), ._1(_1_4), ._2(_2_4), ._3(_3_4), ._4(_4_4), ._5(_5_4), ._6(_6_4), ._7(_7_4),
    ._8(_8_4), ._9(_9_4), .A(A_4), .B(B_4), .C(C_4), .D(D_4), .E(E_4), .F(F_4));

  // Notes on the sheet:
  //   data
  //   clock
  //   encrypted 
  //   4 bit decryption model
  //   Encrypted data  are accepted and then they are decrypted using public and private key to give 4 bit hexadecimal number
  //   DECRYPTION
  //   DECRYPTION
  //   DECRYPTION
  //   DECRYPTION
endmodule

module decryption (
  input  Private_Key,
  input  in_2,
  input  in_3,
  input  in_4,
  input  [3:0] in_5,
  input  in_6,
  input  encrypted,
  input  data,
  input  in_9,
  output _0,
  output _1,
  output _2,
  output _3,
  output _4,
  output _5,
  output _6,
  output _7,
  output _8,
  output _9,
  output A,
  output B,
  output C,
  output D,
  output E,
  output F
);

  wire clock_1_out;

  Clock clock_1 (.out(clock_1_out));
  decoding decoding_1 (
    .Private_Key(Private_Key), .in_2(in_2), .in_3(in_3), .in_4(in_4), .clock(clock_1_out), .in_6(in_5),
    .clock_2(clock_1_out), .encrypted(in_6), .data(encrypted), .in_10(data), .in_11(in_9), ._0(_0), ._1(_1),
    ._2(_2), ._3(_3), ._4(_4), ._5(_5), ._6(_6), ._7(_7), ._8(_8), ._9(_9), .A(A), .B(B), .C(C), .D(D),
    .E(E), .F(F));

  // Notes on the sheet:
  //   Public Key
  //   clock
  //   1 bit decryption model
  //   Decryption
  //   Encrypted data  are accepted and then they are decrypted using public and private key to give 1 bit hexadecimal number
endmodule
