// Logisim project ESF.circ as structural Verilog: 14 circuits, main circuit main
module main (
  output [31:0] L_Out,
  output [31:0] R_Out,
  output halt
);

  wire and_1_out, clock_1_out, nand_1_out, not_1_out, or_1_out;
  wire [1:0] counter_1_q;
  wire [4:0] adder_1_out, counter_2_q;
  wire [15:0] keyschedule_1__15__lsb_0__out, multiplexer_3_out, register_3_q;
  wire [31:0] keyschedule_1_msb_47__16__out, keyschedule_1_msb_79__48__out, multiplexer_1_out,
       multiplexer_2_out, multiplexer_4_out, multiplexer_5_out, ram_1_data, ram_2_data, ram_3_data,
       ram_4_data, ram_5_data, register_1_q, register_2_q, register_4_q, register_5_q, round_1_l_out,
       round_1_r_out;

  RAM #(.addrWidth(3), .dataWidth(32)) ram_1 (
    .addr(3'b100), .data(ram_1_data), .clk(clock_1_out), .ld(1'b1));  // open: sel, clr
  RAM #(.addrWidth(3), .dataWidth(32)) ram_2 (
    .addr(3'b011), .data(ram_2_data), .clk(clock_1_out), .ld(1'b1));  // open: sel, clr
  RAM #(.addrWidth(3), .dataWidth(32)) ram_3 (
    .addr(3'b010), .data(ram_3_data), .clk(clock_1_out), .ld(1'b1));  // open: sel, clr
  RAM #(.addrWidth(3), .dataWidth(32)) ram_4 (
    .addr(3'b001), .data(ram_4_data), .clk(clock_1_out), .ld(1'b1));  // open: sel, clr
  RAM #(.addrWidth(3), .dataWidth(32)) ram_5 (
    .addr(3'b000), .data(ram_5_data), .clk(clock_1_out), .ld(1'b1));  // open: sel, clr
  Counter #(.width(2), .max('h3), .ongoal("stay")) counter_1 (
    .Q(counter_1_q), .clk(clock_1_out));  // open: load, D, count, carry, clr
  Clock clock_1 (.out(clock_1_out));
  and and_1 (and_1_out, counter_1_q[0], counter_1_q[1], clock_1_out);
  Counter #(.width(5), .max('h1f), .ongoal("stay")) counter_2 (
    .Q(counter_2_q), .carry(halt), .clk(and_1_out));  // open: load, D, count, clr
  Multiplexer #(.width(32), .enable("false")) multiplexer_1 (
    .in0({ram_1_data[15:0], ram_2_data[31:16]}), .in1(register_1_q), .out(multiplexer_1_out), .sel(or_1_out));
  Multiplexer #(.width(32), .enable("false")) multiplexer_2 (
    .in0({ram_2_data[15:0], ram_3_data[31:16]}), .in1(register_2_q), .out(multiplexer_2_out), .sel(or_1_out));
  Multiplexer #(.width(16), .enable("false")) multiplexer_3 (
    .in0(ram_3_data[15:0]), .in1(register_3_q), .out(multiplexer_3_out), .sel(or_1_out));
  Multiplexer #(.width(32), .enable("false")) multiplexer_4 (
    .in0(ram_4_data), .in1(register_4_q), .out(multiplexer_4_out), .sel(or_1_out));
  Multiplexer #(.width(32), .enable("false")) multiplexer_5 (
    .in0(ram_5_data), .in1(register_5_q), .out(multiplexer_5_out), .sel(or_1_out));
  or or_1 (or_1_out, counter_2_q[0], counter_2_q[1], counter_2_q[2], counter_2_q[3], counter_2_q[4]);
  Adder #(.width(5)) adder_1 (.a(counter_2_q), .b(5'b00001), .out(adder_1_out));  // open: cin, cout
  KeySchedule keyschedule_1 (
    .MSB_79__48(multiplexer_1_out), .MSB_47__16(multiplexer_2_out), ._15__LSB_0(multiplexer_3_out),
    .in_4(adder_1_out), .MSB_79__48__Out(keyschedule_1_msb_79__48__out),
    .MSB_47__16__Out(keyschedule_1_msb_47__16__out), ._15__LSB_0__Out(keyschedule_1__15__lsb_0__out));
  Round round_1 (
    .L(multiplexer_4_out), .R(multiplexer_5_out), .K(multiplexer_1_out), .R_Out(round_1_r_out),
    .L_Out(round_1_l_out));
  nand nand_1 (nand_1_out, counter_2_q[0], counter_2_q[1], counter_2_q[2], counter_2_q[3], counter_2_q[4]);
  Register #(.width(32)) register_1 (
    .D(keyschedule_1_msb_79__48__out), .en(nand_1_out), .Q(register_1_q), .clk(and_1_out));  // open: clr
  Register #(.width(32)) register_2 (
    .D(keyschedule_1_msb_47__16__out), .en(nand_1_out), .Q(register_2_q), .clk(and_1_out));  // open: clr
  Register #(.width(16)) register_3 (
    .D(keyschedule_1__15__lsb_0__out), .en(nand_1_out), .Q(register_3_q), .clk(and_1_out));  // open: clr
  Register #(.width(32)) register_4 (
    .D(round_1_l_out), .en(nand_1_out), .Q(register_4_q), .clk(and_1_out));  // open: clr
  Register #(.width(32)) register_5 (
    .D(round_1_r_out), .en(nand_1_out), .Q(register_5_q), .clk(and_1_out));  // open: clr
  not not_1 (not_1_out, nand_1_out);
  assign L_Out = not_1_out ? round_1_r_out : 32'bz;  // Controlled_Buffer controlled_buffer_1
  assign R_Out = not_1_out ? round_1_l_out : 32'bz;  // Controlled_Buffer controlled_buffer_2
  // Probe on L_Out
  // Probe on R_Out

  // Notes on the sheet:
  //   16MSBKEY
  //   32MIDDKE MSB KEY
  //   32LSB KEY
  //   32MSB PLAINTEXT
  //   32LSB  PLAINTEXT
endmodule

module XOR32 (
  input  [31:0] in_1,
  input  [31:0] in_2,
  output [31:0] out_3
);

  assign out_3 = in_1 ^ in_2;  // XOR_Gate xor_1, 32 bits wide
endmodule

module S0 (
  input  B3,
  input  B2,
  input  B1,
  input  B0,
  output b3_2,
  output b2_2,
  output b1_2,
  output b0_2
);

  wire and_1_out, and_2_out, and_3_out, and_4_out, and_5_out, and_6_out, and_7_out, and_8_out, and_9_out,
       and_10_out, and_11_out, and_12_out, and_13_out, and_14_out, and_15_out, and_16_out, and_17_out,
       and_18_out, and_19_out, and_20_out, not_1_out, not_2_out, not_3_out, not_4_out, not_5_out, not_6_out,
       not_7_out, not_8_out, not_9_out, not_10_out, not_11_out, not_12_out, not_13_out, not_14_out,
       not_15_out, not_16_out, not_17_out, not_18_out, not_19_out, not_20_out, not_21_out, not_22_out,
       not_23_out, not_24_out, not_25_out, not_26_out, not_27_out, not_28_out, not_29_out, not_30_out,
       not_31_out, not_32_out, not_33_out, not_34_out;

  not not_1 (not_1_out, B2);
  not not_2 (not_2_out, B1);
  not not_3 (not_3_out, B3);
  not not_4 (not_4_out, B2);
  not not_5 (not_5_out, B0);
  not not_6 (not_6_out, B3);
  not not_7 (not_7_out, B1);
  not not_8 (not_8_out, B0);
  not not_9 (not_9_out, B2);
  not not_10 (not_10_out, B1);
  not not_11 (not_11_out, B3);
  not not_12 (not_12_out, B0);
  not not_13 (not_13_out, B3);
  not not_14 (not_14_out, B1);
  not not_15 (not_15_out, B2);
  not not_16 (not_16_out, B1);
  not not_17 (not_17_out, B2);
  not not_18 (not_18_out, B0);
  not not_19 (not_19_out, B1);
  not not_20 (not_20_out, B0);
  not not_21 (not_21_out, B3);
  not not_22 (not_22_out, B2);
  not not_23 (not_23_out, B0);
  not not_24 (not_24_out, B1);
  not not_25 (not_25_out, B0);
  not not_26 (not_26_out, B3);
  not not_27 (not_27_out, B2);
  not not_28 (not_28_out, B3);
  not not_29 (not_29_out, B2);
  not not_30 (not_30_out, B0);
  not not_31 (not_31_out, B3);
  not not_32 (not_32_out, B2);
  not not_33 (not_33_out, B1);
  not not_34 (not_34_out, B0);
  and and_1 (and_1_out, not_1_out, not_2_out, B0);
  and and_2 (and_2_out, not_3_out, not_4_out, B1, not_5_out);
  and and_3 (and_3_out, not_6_out, B2, not_7_out, not_8_out);
  and and_4 (and_4_out, B2, B1, B0);
  and and_5 (and_5_out, B3, not_9_out, not_10_out);
  and and_6 (and_6_out, B3, B2, B1);
  and and_7 (and_7_out, not_11_out, B1, not_12_out);
  and and_8 (and_8_out, not_13_out, B2, not_14_out, B0);
  and and_9 (and_9_out, B3, not_15_out, not_16_out);
  and and_10 (and_10_out, B3, not_17_out, not_18_out);
  and and_11 (and_11_out, B3, not_19_out, not_20_out);
  and and_12 (and_12_out, B3, B2, B1, B0);
  and and_13 (and_13_out, not_21_out, not_22_out, not_23_out);
  and and_14 (and_14_out, not_24_out, not_25_out);
  and and_15 (and_15_out, not_26_out, B2, B0);
  and and_16 (and_16_out, B3, not_27_out, B1, B0);
  and and_17 (and_17_out, not_28_out, not_29_out, not_30_out);
  and and_18 (and_18_out, not_31_out, B1);
  and and_19 (and_19_out, B3, not_32_out, not_33_out, B0);
  and and_20 (and_20_out, B3, B2, not_34_out);
  or or_1 (b3_2, and_1_out, and_2_out, and_3_out, and_4_out, and_5_out, and_6_out);
  or or_2 (b2_2, and_7_out, and_8_out, and_9_out, and_10_out, and_11_out, and_12_out);
  or or_3 (b1_2, and_13_out, and_14_out, and_15_out, and_16_out);
  or or_4 (b0_2, and_17_out, and_18_out, and_19_out, and_20_out);
endmodule

module S1 (
  input  B3,
  input  B2,
  input  B1,
  input  B0,
  output b3_2,
  output b2_2,
  output b1_2,
  output b0_2
);

  wire and_1_out, and_2_out, and_3_out, and_4_out, and_5_out, and_6_out, and_7_out, and_8_out, and_9_out,
       and_10_out, and_11_out, and_12_out, and_13_out, and_14_out, and_15_out, and_16_out, and_17_out,
       and_18_out, and_19_out, and_20_out, and_21_out, not_1_out, not_2_out, not_3_out, not_4_out, not_5_out,
       not_6_out, not_7_out, not_8_out, not_9_out, not_10_out, not_11_out, not_12_out, not_13_out,
       not_14_out, not_15_out, not_16_out, not_17_out, not_18_out, not_19_out, not_20_out, not_21_out,
       not_22_out, not_23_out, not_24_out, not_25_out, not_26_out, not_27_out, not_28_out, not_29_out,
       not_30_out, not_31_out, not_32_out, not_33_out, not_34_out, not_35_out, not_36_out, not_37_out,
       not_38_out;

  not not_1 (not_1_out, B3);
  not not_2 (not_2_out, B2);
  not not_3 (not_3_out, B1);
  not not_4 (not_4_out, B3);
  not not_5 (not_5_out, B1);
  not not_6 (not_6_out, B0);
  not not_7 (not_7_out, B3);
  not not_8 (not_8_out, B1);
  not not_9 (not_9_out, B2);
  not not_10 (not_10_out, B3);
  not not_11 (not_11_out, B2);
  not not_12 (not_12_out, B1);
  not not_13 (not_13_out, B3);
  not not_14 (not_14_out, B2);
  not not_15 (not_15_out, B3);
  not not_16 (not_16_out, B0);
  not not_17 (not_17_out, B2);
  not not_18 (not_18_out, B0);
  not not_19 (not_19_out, B1);
  not not_20 (not_20_out, B3);
  not not_21 (not_21_out, B2);
  not not_22 (not_22_out, B0);
  not not_23 (not_23_out, B2);
  not not_24 (not_24_out, B0);
  not not_25 (not_25_out, B3);
  not not_26 (not_26_out, B2);
  not not_27 (not_27_out, B1);
  not not_28 (not_28_out, B0);
  not not_29 (not_29_out, B3);
  not not_30 (not_30_out, B1);
  not not_31 (not_31_out, B0);
  not not_32 (not_32_out, B2);
  not not_33 (not_33_out, B1);
  not not_34 (not_34_out, B0);
  not not_35 (not_35_out, B3);
  not not_36 (not_36_out, B2);
  not not_37 (not_37_out, B0);
  not not_38 (not_38_out, B1);
  and and_1 (and_1_out, not_1_out, not_2_out, not_3_out);
  and and_2 (and_2_out, not_4_out, not_5_out, not_6_out);
  and and_3 (and_3_out, not_7_out, B2, B1, B0);
  and and_4 (and_4_out, B3, not_8_out, B0);
  and and_5 (and_5_out, B3, not_9_out, B1);
  and and_6 (and_6_out, not_10_out, not_11_out, not_12_out);
  and and_7 (and_7_out, not_13_out, not_14_out, B0);
  and and_8 (and_8_out, not_15_out, B2, B1, not_16_out);
  and and_9 (and_9_out, B3, not_17_out, B1, not_18_out);
  and and_10 (and_10_out, B3, B2, not_19_out);
  and and_11 (and_11_out, B3, B2, B0);
  and and_12 (and_12_out, not_20_out, not_21_out, not_22_out);
  and and_13 (and_13_out, not_23_out, B1, not_24_out);
  and and_14 (and_14_out, not_25_out, B1, B0);
  and and_15 (and_15_out, B3, not_26_out, not_27_out, B0);
  and and_16 (and_16_out, B3, B2, not_28_out);
  and and_17 (and_17_out, not_29_out, not_30_out, not_31_out);
  and and_18 (and_18_out, not_32_out, not_33_out, not_34_out);
  and and_19 (and_19_out, not_35_out, not_36_out, B1, B0);
  and and_20 (and_20_out, B2, B1, not_37_out);
  and and_21 (and_21_out, B3, not_38_out, B0);
  or or_1 (b3_2, and_1_out, and_2_out, and_3_out, and_4_out, and_5_out);
  or or_2 (b2_2, and_6_out, and_7_out, and_8_out, and_9_out, and_10_out, and_11_out);
  or or_3 (b1_2, and_12_out, and_13_out, and_14_out, and_15_out, and_16_out);
  or or_4 (b0_2, and_17_out, and_18_out, and_19_out, and_20_out, and_21_out);
endmodule

module F (
  input  [31:0] MSB_63_32,
  input  [31:0] _31_0,
  output [31:0] _31_0_Out
);

  wire [31:0] xor_1_out;

  assign xor_1_out = MSB_63_32 ^ _31_0;  // XOR_Gate xor_1, 32 bits wide
  S7 s7_1 (
    .B3(xor_1_out[31]), .B2(xor_1_out[30]), .B1(xor_1_out[29]), .B0(xor_1_out[28]), .b3_2(_31_0_Out[31]),
    .b2_2(_31_0_Out[23]), .b1_2(_31_0_Out[15]), .b0_2(_31_0_Out[7]));
  S6 s6_1 (
    .B3(xor_1_out[27]), .B2(xor_1_out[26]), .B1(xor_1_out[25]), .B0(xor_1_out[24]), .b3_2(_31_0_Out[30]),
    .b2_2(_31_0_Out[22]), .b1_2(_31_0_Out[14]), .b0_2(_31_0_Out[6]));
  S5 s5_1 (
    .B3(xor_1_out[23]), .B2(xor_1_out[22]), .B1(xor_1_out[21]), .B0(xor_1_out[20]), .b3_2(_31_0_Out[29]),
    .b2_2(_31_0_Out[21]), .b1_2(_31_0_Out[13]), .b0_2(_31_0_Out[5]));
  S4 s4_1 (
    .B3(xor_1_out[19]), .B2(xor_1_out[18]), .B1(xor_1_out[17]), .B0(xor_1_out[16]), .b0_2(_31_0_Out[28]),
    .b1_2(_31_0_Out[20]), .b2_2(_31_0_Out[12]), .b3_2(_31_0_Out[4]));
  S3 s3_1 (
    .B3(xor_1_out[15]), .B2(xor_1_out[14]), .B1(xor_1_out[13]), .B0(xor_1_out[12]), .b0_2(_31_0_Out[27]),
    .b1_2(_31_0_Out[19]), .b2_2(_31_0_Out[11]), .b3_2(_31_0_Out[3]));
  S2 s2_1 (
    .B3(xor_1_out[11]), .B2(xor_1_out[10]), .B1(xor_1_out[9]), .B0(xor_1_out[8]), .b3_2(_31_0_Out[26]),
    .b2_2(_31_0_Out[18]), .b1_2(_31_0_Out[10]), .b0_2(_31_0_Out[2]));
  S1 s1_1 (
    .B3(xor_1_out[7]), .B2(xor_1_out[6]), .B1(xor_1_out[5]), .B0(xor_1_out[4]), .b3_2(_31_0_Out[25]),
    .b2_2(_31_0_Out[17]), .b1_2(_31_0_Out[9]), .b0_2(_31_0_Out[1]));
  S0 s0_1 (
    .B3(xor_1_out[3]), .B2(xor_1_out[2]), .B1(xor_1_out[1]), .B0(xor_1_out[0]), .b3_2(_31_0_Out[24]),
    .b2_2(_31_0_Out[16]), .b1_2(_31_0_Out[8]), .b0_2(_31_0_Out[0]));

  // Other names for the same wires on the sheet: _0 = _31_0_Out[0]; _1 = _31_0_Out[1]; _2 = _31_0_Out[2];
  //   _3 = _31_0_Out[3]; _4 = _31_0_Out[4]; _5 = _31_0_Out[5]; _6 = _31_0_Out[6]; _7 = _31_0_Out[7];
  //   _8 = _31_0_Out[8]; _9 = _31_0_Out[9]; _10 = _31_0_Out[10]; _11 = _31_0_Out[11]; _12 = _31_0_Out[12];
  //   _13 = _31_0_Out[13]; _14 = _31_0_Out[14]; _15 = _31_0_Out[15]; _16 = _31_0_Out[16]; _17 = _31_0_Out[17];
  //   _18 = _31_0_Out[18]; _19 = _31_0_Out[19]; _20 = _31_0_Out[20]; _21 = _31_0_Out[21]; _22 = _31_0_Out[22];
  //   _23 = _31_0_Out[23]; _24 = _31_0_Out[24]; _25 = _31_0_Out[25]; _26 = _31_0_Out[26]; _27 = _31_0_Out[27];
  //   _28 = _31_0_Out[28]; _29 = _31_0_Out[29]; _30 = _31_0_Out[30]; _31 = _31_0_Out[31]

  // Notes on the sheet:
  //   S-Box
  //   P-Box
endmodule

module Round (
  input  [31:0] L,
  input  [31:0] R,
  input  [31:0] K,
  output [31:0] R_Out,
  output [31:0] L_Out
);

  wire [31:0] f_1__31_0_out, shifter_1_out;

  Shifter #(.width(32), .shift("rl")) shifter_1 (.in(L), .\dist (5'b00111), .out(shifter_1_out));
  XOR32 xor32_1 (.in_1(f_1__31_0_out), .in_2(shifter_1_out), .out_3(R_Out));
  F f_1 (.MSB_63_32(K), ._31_0(R), ._31_0_Out(f_1__31_0_out));

  assign L_Out = R;
endmodule

module KeySchedule (
  input  [31:0] MSB_79__48,
  input  [31:0] MSB_47__16,
  input  [15:0] _15__LSB_0,
  input  [4:0] in_4,
  output [31:0] MSB_79__48__Out,
  output [31:0] MSB_47__16__Out,
  output [15:0] _15__LSB_0__Out
);

  wire rotate_1_out_4, rotate_1_out_5, rotate_1_out_6, rotate_1_out_7, rotate_1_out_8, rotate_1_out_9,
       rotate_1_out_10, rotate_1_out_11;
  wire [4:0] rotate_1_out_40;

  Rotate rotate_1 (
    .MSB_79__48(MSB_79__48), .MSB_47__16(MSB_47__16), ._15__LSB_0(_15__LSB_0), .out_4(rotate_1_out_4),
    .out_5(rotate_1_out_5), .out_6(rotate_1_out_6), .out_7(rotate_1_out_7), .out_8(rotate_1_out_8),
    .out_9(rotate_1_out_9), .out_10(rotate_1_out_10), .out_11(rotate_1_out_11), .out_12(MSB_79__48__Out[23]),
    .out_13(MSB_79__48__Out[22]), .out_14(MSB_79__48__Out[21]), .out_15(MSB_79__48__Out[20]),
    .out_16(MSB_79__48__Out[19]), .out_17(MSB_79__48__Out[18]), .out_18(MSB_79__48__Out[17]),
    .out_19(MSB_79__48__Out[16]), .out_20(MSB_79__48__Out[15]), .out_21(MSB_79__48__Out[14]),
    .out_22(MSB_79__48__Out[13]), .out_23(MSB_79__48__Out[12]), .out_24(MSB_79__48__Out[11]),
    .out_25(MSB_79__48__Out[10]), .out_26(MSB_79__48__Out[9]), .out_27(MSB_79__48__Out[8]),
    .out_28(MSB_79__48__Out[7]), .out_29(MSB_79__48__Out[6]), .out_30(MSB_79__48__Out[5]),
    .out_31(MSB_79__48__Out[4]), .out_32(MSB_79__48__Out[3]), .out_33(MSB_79__48__Out[2]),
    .out_34(MSB_79__48__Out[1]), .out_35(MSB_79__48__Out[0]), .out_36(rotate_1_out_40[4]),
    .out_37(rotate_1_out_40[3]), .out_38(rotate_1_out_40[2]), .out_39(rotate_1_out_40[1]),
    .out_40(rotate_1_out_40[0]), .out_41(MSB_47__16__Out[26]), .out_42(MSB_47__16__Out[25]),
    .out_43(MSB_47__16__Out[24]), .out_44(MSB_47__16__Out[23]), .out_45(MSB_47__16__Out[22]),
    .out_46(MSB_47__16__Out[21]), .out_47(MSB_47__16__Out[20]), .out_48(MSB_47__16__Out[19]),
    .out_49(MSB_47__16__Out[18]), .out_50(MSB_47__16__Out[17]), .out_51(MSB_47__16__Out[16]),
    .out_52(MSB_47__16__Out[15]), .out_53(MSB_47__16__Out[14]), .out_54(MSB_47__16__Out[13]),
    .out_55(MSB_47__16__Out[12]), .out_56(MSB_47__16__Out[11]), .out_57(MSB_47__16__Out[10]),
    .out_58(MSB_47__16__Out[9]), .out_59(MSB_47__16__Out[8]), .out_60(MSB_47__16__Out[7]),
    .out_61(MSB_47__16__Out[6]), .out_62(MSB_47__16__Out[5]), .out_63(MSB_47__16__Out[4]),
    .out_64(MSB_47__16__Out[3]), .out_65(MSB_47__16__Out[2]), .out_66(MSB_47__16__Out[1]),
    .out_67(MSB_47__16__Out[0]), .out_68(_15__LSB_0__Out[15]), .out_69(_15__LSB_0__Out[14]),
    .out_70(_15__LSB_0__Out[13]), .out_71(_15__LSB_0__Out[12]), .out_72(_15__LSB_0__Out[11]),
    .out_73(_15__LSB_0__Out[10]), .out_74(_15__LSB_0__Out[9]), .out_75(_15__LSB_0__Out[8]),
    .out_76(_15__LSB_0__Out[7]), .out_77(_15__LSB_0__Out[6]), .out_78(_15__LSB_0__Out[5]),
    .out_79(_15__LSB_0__Out[4]), .out_80(_15__LSB_0__Out[3]), .out_81(_15__LSB_0__Out[2]),
    .out_82(_15__LSB_0__Out[1]), .out_83(_15__LSB_0__Out[0]));
  S0 s0_1 (
    .B3(rotate_1_out_4), .B2(rotate_1_out_5), .B1(rotate_1_out_6), .B0(rotate_1_out_7),
    .b3_2(MSB_79__48__Out[31]), .b2_2(MSB_79__48__Out[30]), .b1_2(MSB_79__48__Out[29]),
    .b0_2(MSB_79__48__Out[28]));
  S0 s0_2 (
    .B3(rotate_1_out_8), .B2(rotate_1_out_9), .B1(rotate_1_out_10), .B0(rotate_1_out_11),
    .b3_2(MSB_79__48__Out[27]), .b2_2(MSB_79__48__Out[26]), .b1_2(MSB_79__48__Out[25]),
    .b0_2(MSB_79__48__Out[24]));
  assign MSB_47__16__Out[31:27] = rotate_1_out_40 ^ in_4;  // XOR_Gate xor_1, 5 bits wide
endmodule

module S2 (
  input  B3,
  input  B2,
  input  B1,
  input  B0,
  output b3_2,
  output b2_2,
  output b1_2,
  output b0_2
);

  wire and_1_out, and_2_out, and_3_out, and_4_out, and_5_out, and_6_out, and_7_out, and_8_out, and_9_out,
       and_10_out, and_11_out, and_12_out, and_13_out, and_14_out, and_15_out, and_16_out, and_17_out,
       and_18_out, and_19_out, and_20_out, and_21_out, and_22_out, not_1_out, not_2_out, not_3_out,
       not_4_out, not_5_out, not_6_out, not_7_out, not_8_out, not_9_out, not_10_out, not_11_out, not_12_out,
       not_13_out, not_14_out, not_15_out, not_16_out, not_17_out, not_18_out, not_19_out, not_20_out,
       not_21_out, not_22_out, not_23_out, not_24_out, not_25_out, not_26_out, not_27_out, not_28_out,
       not_29_out, not_30_out, not_31_out, not_32_out, not_33_out, not_34_out, not_35_out;

  not not_1 (not_1_out, B2);
  not not_2 (not_2_out, B1);
  not not_3 (not_3_out, B0);
  not not_4 (not_4_out, B3);
  not not_5 (not_5_out, B1);
  not not_6 (not_6_out, B3);
  not not_7 (not_7_out, B2);
  not not_8 (not_8_out, B0);
  not not_9 (not_9_out, B3);
  not not_10 (not_10_out, B1);
  not not_11 (not_11_out, B2);
  not not_12 (not_12_out, B0);
  not not_13 (not_13_out, B3);
  not not_14 (not_14_out, B2);
  not not_15 (not_15_out, B0);
  not not_16 (not_16_out, B2);
  not not_17 (not_17_out, B0);
  not not_18 (not_18_out, B3);
  not not_19 (not_19_out, B2);
  not not_20 (not_20_out, B1);
  not not_21 (not_21_out, B2);
  not not_22 (not_22_out, B0);
  not not_23 (not_23_out, B3);
  not not_24 (not_24_out, B0);
  not not_25 (not_25_out, B3);
  not not_26 (not_26_out, B3);
  not not_27 (not_27_out, B2);
  not not_28 (not_28_out, B3);
  not not_29 (not_29_out, B3);
  not not_30 (not_30_out, B1);
  not not_31 (not_31_out, B0);
  not not_32 (not_32_out, B2);
  not not_33 (not_33_out, B1);
  not not_34 (not_34_out, B1);
  not not_35 (not_35_out, B0);
  and and_1 (and_1_out, not_1_out, not_2_out, not_3_out);
  and and_2 (and_2_out, not_4_out, B1, B0);
  and and_3 (and_3_out, B2, not_5_out, B0);
  and and_4 (and_4_out, not_6_out, B2, B1);
  and and_5 (and_5_out, B3, not_7_out, not_8_out);
  and and_6 (and_6_out, not_9_out, not_10_out, B0);
  and and_7 (and_7_out, not_11_out, B1, not_12_out);
  and and_8 (and_8_out, not_13_out, B2, B0);
  and and_9 (and_9_out, B3, not_14_out, not_15_out);
  and and_10 (and_10_out, B3, not_16_out, B1);
  and and_11 (and_11_out, B3, B1, not_17_out);
  and and_12 (and_12_out, not_18_out, not_19_out, not_20_out, B0);
  and and_13 (and_13_out, not_21_out, B1, not_22_out);
  and and_14 (and_14_out, not_23_out, B2, not_24_out);
  and and_15 (and_15_out, not_25_out, B2, B1);
  and and_16 (and_16_out, B3, B2, B0);
  and and_17 (and_17_out, not_26_out, not_27_out, B1);
  and and_18 (and_18_out, not_28_out, B1, B0);
  and and_19 (and_19_out, not_29_out, B2, not_30_out, not_31_out);
  and and_20 (and_20_out, B3, not_32_out, not_33_out);
  and and_21 (and_21_out, B3, not_34_out, B0);
  and and_22 (and_22_out, B3, B2, B1, not_35_out);
  or or_1 (b3_2, and_1_out, and_2_out, and_3_out, and_4_out, and_5_out);
  or or_2 (b2_2, and_6_out, and_7_out, and_8_out, and_9_out, and_10_out, and_11_out);
  or or_3 (b1_2, and_12_out, and_13_out, and_14_out, and_15_out, and_16_out);
  or or_4 (b0_2, and_17_out, and_18_out, and_19_out, and_20_out, and_21_out, and_22_out);
endmodule

module S3 (
  input  B3,
  input  B2,
  input  B1,
  input  B0,
  output b0_2,
  output b1_2,
  output b2_2,
  output b3_2
);

  wire and_1_out, and_2_out, and_3_out, and_4_out, and_5_out, and_6_out, and_7_out, and_8_out, and_9_out,
       and_10_out, and_11_out, and_12_out, and_13_out, and_14_out, and_15_out, and_16_out, and_17_out,
       and_18_out, and_19_out, and_20_out, and_21_out, not_1_out, not_2_out, not_3_out, not_4_out, not_5_out,
       not_6_out, not_7_out, not_8_out, not_9_out, not_10_out, not_11_out, not_12_out, not_13_out,
       not_14_out, not_15_out, not_16_out, not_17_out, not_18_out, not_19_out, not_20_out, not_21_out,
       not_22_out, not_23_out, not_24_out, not_25_out, not_26_out, not_27_out, not_28_out, not_29_out,
       not_30_out, not_31_out, not_32_out;

  not not_1 (not_1_out, B3);
  not not_2 (not_2_out, B2);
  not not_3 (not_3_out, B3);
  not not_4 (not_4_out, B2);
  not not_5 (not_5_out, B3);
  not not_6 (not_6_out, B1);
  not not_7 (not_7_out, B1);
  not not_8 (not_8_out, B0);
  not not_9 (not_9_out, B3);
  not not_10 (not_10_out, B2);
  not not_11 (not_11_out, B1);
  not not_12 (not_12_out, B3);
  not not_13 (not_13_out, B0);
  not not_14 (not_14_out, B0);
  not not_15 (not_15_out, B2);
  not not_16 (not_16_out, B1);
  not not_17 (not_17_out, B0);
  not not_18 (not_18_out, B3);
  not not_19 (not_19_out, B2);
  not not_20 (not_20_out, B1);
  not not_21 (not_21_out, B2);
  not not_22 (not_22_out, B0);
  not not_23 (not_23_out, B3);
  not not_24 (not_24_out, B1);
  not not_25 (not_25_out, B1);
  not not_26 (not_26_out, B3);
  not not_27 (not_27_out, B2);
  not not_28 (not_28_out, B0);
  not not_29 (not_29_out, B3);
  not not_30 (not_30_out, B2);
  not not_31 (not_31_out, B1);
  not not_32 (not_32_out, B0);
  and and_1 (and_1_out, not_1_out, not_2_out, B0);
  and and_2 (and_2_out, not_3_out, not_4_out, B1);
  and and_3 (and_3_out, not_5_out, B2, not_6_out);
  and and_4 (and_4_out, B3, not_7_out, not_8_out);
  and and_5 (and_5_out, B3, B2, B1, B0);
  and and_6 (and_6_out, not_9_out, not_10_out, not_11_out, B0);
  and and_7 (and_7_out, not_12_out, B2, not_13_out);
  and and_8 (and_8_out, B2, B1, not_14_out);
  and and_9 (and_9_out, B3, not_15_out, not_16_out, not_17_out);
  and and_10 (and_10_out, B3, B1, B0);
  and and_11 (and_11_out, B3, B2, B0);
  and and_12 (and_12_out, not_18_out, not_19_out, not_20_out, B0);
  and and_13 (and_13_out, not_21_out, B1, not_22_out);
  and and_14 (and_14_out, not_23_out, B2, B1);
  and and_15 (and_15_out, B3, B2, not_24_out);
  and and_16 (and_16_out, B3, B2, B0);
  and and_17 (and_17_out, not_25_out, B0);
  and and_18 (and_18_out, not_26_out, not_27_out, B1, not_28_out);
  and and_19 (and_19_out, not_29_out, B2, B0);
  and and_20 (and_20_out, B3, not_30_out, not_31_out);
  and and_21 (and_21_out, B3, B2, B1, not_32_out);
  or or_1 (b0_2, and_1_out, and_2_out, and_3_out, and_4_out, and_5_out);
  or or_2 (b1_2, and_6_out, and_7_out, and_8_out, and_9_out, and_10_out, and_11_out);
  or or_3 (b2_2, and_12_out, and_13_out, and_14_out, and_15_out, and_16_out);
  or or_4 (b3_2, and_17_out, and_18_out, and_19_out, and_20_out, and_21_out);
endmodule

module S4 (
  input  B3,
  input  B2,
  input  B1,
  input  B0,
  output b0_2,
  output b1_2,
  output b2_2,
  output b3_2
);

  wire and_1_out, and_2_out, and_3_out, and_4_out, and_5_out, and_6_out, and_7_out, and_8_out, and_9_out,
       and_10_out, and_11_out, and_12_out, and_13_out, and_14_out, and_15_out, and_16_out, and_17_out,
       and_18_out, and_19_out, and_20_out, and_21_out, and_22_out, not_1_out, not_2_out, not_3_out,
       not_4_out, not_5_out, not_6_out, not_7_out, not_8_out, not_9_out, not_10_out, not_11_out, not_12_out,
       not_13_out, not_14_out, not_15_out, not_16_out, not_17_out, not_18_out, not_19_out, not_20_out,
       not_21_out, not_22_out, not_23_out, not_24_out, not_25_out, not_26_out, not_27_out, not_28_out,
       not_29_out, not_30_out, not_31_out, not_32_out, not_33_out;

  not not_1 (not_1_out, B3);
  not not_2 (not_2_out, B2);
  not not_3 (not_3_out, B1);
  not not_4 (not_4_out, B3);
  not not_5 (not_5_out, B0);
  not not_6 (not_6_out, B1);
  not not_7 (not_7_out, B0);
  not not_8 (not_8_out, B1);
  not not_9 (not_9_out, B2);
  not not_10 (not_10_out, B1);
  not not_11 (not_11_out, B3);
  not not_12 (not_12_out, B1);
  not not_13 (not_13_out, B0);
  not not_14 (not_14_out, B1);
  not not_15 (not_15_out, B0);
  not not_16 (not_16_out, B3);
  not not_17 (not_17_out, B2);
  not not_18 (not_18_out, B2);
  not not_19 (not_19_out, B3);
  not not_20 (not_20_out, B0);
  not not_21 (not_21_out, B2);
  not not_22 (not_22_out, B1);
  not not_23 (not_23_out, B0);
  not not_24 (not_24_out, B1);
  not not_25 (not_25_out, B3);
  not not_26 (not_26_out, B2);
  not not_27 (not_27_out, B1);
  not not_28 (not_28_out, B3);
  not not_29 (not_29_out, B2);
  not not_30 (not_30_out, B2);
  not not_31 (not_31_out, B1);
  not not_32 (not_32_out, B0);
  not not_33 (not_33_out, B0);
  and and_1 (and_1_out, not_1_out, not_2_out, not_3_out, B0);
  and and_2 (and_2_out, not_4_out, B1, not_5_out);
  and and_3 (and_3_out, B2, not_6_out, not_7_out);
  and and_4 (and_4_out, B3, B1, B0);
  and and_5 (and_5_out, B3, B2, not_8_out);
  and and_6 (and_6_out, not_9_out, not_10_out, B0);
  and and_7 (and_7_out, not_11_out, B2, not_12_out, not_13_out);
  and and_8 (and_8_out, B2, B1, B0);
  and and_9 (and_9_out, B3, not_14_out, B0);
  and and_10 (and_10_out, B3, B1, not_15_out);
  and and_11 (and_11_out, not_16_out, not_17_out, B0);
  and and_12 (and_12_out, not_18_out, B1, B0);
  and and_13 (and_13_out, not_19_out, B2, B1);
  and and_14 (and_14_out, B2, B1, not_20_out);
  and and_15 (and_15_out, B3, not_21_out, not_22_out, not_23_out);
  and and_16 (and_16_out, B3, B2, not_24_out, B0);
  and and_17 (and_17_out, not_25_out, not_26_out, not_27_out);
  and and_18 (and_18_out, not_28_out, not_29_out, B0);
  and and_19 (and_19_out, not_30_out, not_31_out, B0);
  and and_20 (and_20_out, B2, B1, not_32_out);
  and and_21 (and_21_out, B3, B2, not_33_out);
  and and_22 (and_22_out, B3, B2, B1);
  or or_1 (b0_2, and_1_out, and_2_out, and_3_out, and_4_out, and_5_out);
  or or_2 (b1_2, and_6_out, and_7_out, and_8_out, and_9_out, and_10_out);
  or or_3 (b2_2, and_11_out, and_12_out, and_13_out, and_14_out, and_15_out, and_16_out);
  or or_4 (b3_2, and_17_out, and_18_out, and_19_out, and_20_out, and_21_out, and_22_out);
endmodule

module S5 (
  input  B3,
  input  B2,
  input  B1,
  input  B0,
  output b3_2,
  output b2_2,
  output b1_2,
  output b0_2
);

  wire and_1_out, and_2_out, and_3_out, and_4_out, and_5_out, and_6_out, and_7_out, and_8_out, and_9_out,
       and_10_out, and_11_out, and_12_out, and_13_out, and_14_out, and_15_out, and_16_out, and_17_out,
       and_18_out, and_19_out, and_20_out, and_21_out, and_22_out, not_1_out, not_2_out, not_3_out,
       not_4_out, not_5_out, not_6_out, not_7_out, not_8_out, not_9_out, not_10_out, not_11_out, not_12_out,
       not_13_out, not_14_out, not_15_out, not_16_out, not_17_out, not_18_out, not_19_out, not_20_out,
       not_21_out, not_22_out, not_23_out, not_24_out, not_25_out, not_26_out, not_27_out, not_28_out,
       not_29_out, not_30_out, not_31_out, not_32_out, not_33_out, not_34_out, not_35_out, not_36_out;

  not not_1 (not_1_out, B3);
  not not_2 (not_2_out, B2);
  not not_3 (not_3_out, B1);
  not not_4 (not_4_out, B0);
  not not_5 (not_5_out, B3);
  not not_6 (not_6_out, B3);
  not not_7 (not_7_out, B3);
  not not_8 (not_8_out, B2);
  not not_9 (not_9_out, B1);
  not not_10 (not_10_out, B0);
  not not_11 (not_11_out, B3);
  not not_12 (not_12_out, B2);
  not not_13 (not_13_out, B1);
  not not_14 (not_14_out, B3);
  not not_15 (not_15_out, B1);
  not not_16 (not_16_out, B0);
  not not_17 (not_17_out, B3);
  not not_18 (not_18_out, B0);
  not not_19 (not_19_out, B1);
  not not_20 (not_20_out, B3);
  not not_21 (not_21_out, B2);
  and and_1 (and_1_out, not_20_out, not_21_out, not_22_out);
  not not_22 (not_22_out, B0);
  not not_23 (not_23_out, B3);
  and and_2 (and_2_out, not_23_out, not_24_out, B1);
  not not_24 (not_24_out, B2);
  and and_3 (and_3_out, B2, not_25_out, B0);
  not not_25 (not_25_out, B1);
  not not_26 (not_26_out, B1);
  and and_4 (and_4_out, B3, not_26_out, B0);
  and and_5 (and_5_out, B3, B1, not_27_out);
  not not_27 (not_27_out, B0);
  not not_28 (not_28_out, B3);
  and and_6 (and_6_out, not_28_out, not_29_out, not_30_out);
  not not_29 (not_29_out, B2);
  not not_30 (not_30_out, B1);
  not not_31 (not_31_out, B3);
  and and_7 (and_7_out, not_31_out, not_32_out, B0);
  not not_32 (not_32_out, B2);
  not not_33 (not_33_out, B2);
  not not_34 (not_34_out, B1);
  and and_8 (and_8_out, not_33_out, not_34_out, B0);
  and and_9 (and_9_out, B2, B1, not_35_out);
  not not_35 (not_35_out, B0);
  and and_10 (and_10_out, B3, B2, not_36_out);
  not not_36 (not_36_out, B0);
  and and_11 (and_11_out, B3, B2, B1);
  and and_12 (and_12_out, not_1_out, not_2_out, not_3_out, not_4_out);
  and and_13 (and_13_out, not_5_out, B1, B0);
  and and_14 (and_14_out, not_6_out, B2, B0);
  and and_15 (and_15_out, not_7_out, B2, B1);
  and and_16 (and_16_out, B3, not_8_out, B1);
  and and_17 (and_17_out, B3, B2, not_9_out, not_10_out);
  and and_18 (and_18_out, not_11_out, not_12_out, not_13_out);
  and and_19 (and_19_out, not_14_out, not_15_out, not_16_out);
  and and_20 (and_20_out, not_17_out, B2, B1, B0);
  and and_21 (and_21_out, B3, B1, not_18_out);
  and and_22 (and_22_out, B3, B2, not_19_out);
  or or_1 (b1_2, and_1_out, and_2_out, and_3_out, and_4_out, and_5_out);
  or or_2 (b3_2, and_12_out, and_13_out, and_14_out, and_15_out, and_16_out, and_17_out);
  or or_3 (b2_2, and_18_out, and_19_out, and_20_out, and_21_out, and_22_out);
  or or_4 (b0_2, and_6_out, and_7_out, and_8_out, and_9_out, and_10_out, and_11_out);
endmodule

module S6 (
  input  B3,
  input  B2,
  input  B1,
  input  B0,
  output b3_2,
  output b2_2,
  output b1_2,
  output b0_2
);

  wire and_1_out, and_2_out, and_3_out, and_4_out, and_5_out, and_6_out, and_7_out, and_8_out, and_9_out,
       and_10_out, and_11_out, and_12_out, and_13_out, and_14_out, and_15_out, and_16_out, and_17_out,
       and_18_out, and_19_out, and_20_out, and_21_out, and_22_out, not_1_out, not_2_out, not_3_out,
       not_4_out, not_5_out, not_6_out, not_7_out, not_8_out, not_9_out, not_10_out, not_11_out, not_12_out,
       not_13_out, not_14_out, not_15_out, not_16_out, not_17_out, not_18_out, not_19_out, not_20_out,
       not_21_out, not_22_out, not_23_out, not_24_out, not_25_out, not_26_out, not_27_out, not_28_out,
       not_29_out, not_30_out, not_31_out, not_32_out, not_33_out, not_34_out, not_35_out, not_36_out,
       not_37_out, not_38_out;

  not not_1 (not_1_out, B3);
  not not_2 (not_2_out, B2);
  not not_3 (not_3_out, B0);
  not not_4 (not_4_out, B1);
  not not_5 (not_5_out, B0);
  not not_6 (not_6_out, B3);
  not not_7 (not_7_out, B2);
  not not_8 (not_8_out, B1);
  not not_9 (not_9_out, B2);
  not not_10 (not_10_out, B0);
  not not_11 (not_11_out, B3);
  not not_12 (not_12_out, B2);
  not not_13 (not_13_out, B0);
  not not_14 (not_14_out, B3);
  not not_15 (not_15_out, B0);
  not not_16 (not_16_out, B2);
  not not_17 (not_17_out, B3);
  not not_18 (not_18_out, B1);
  not not_19 (not_19_out, B1);
  not not_20 (not_20_out, B0);
  not not_21 (not_21_out, B3);
  not not_22 (not_22_out, B2);
  not not_23 (not_23_out, B1);
  not not_24 (not_24_out, B2);
  not not_25 (not_25_out, B1);
  not not_26 (not_26_out, B0);
  not not_27 (not_27_out, B3);
  not not_28 (not_28_out, B0);
  not not_29 (not_29_out, B2);
  not not_30 (not_30_out, B1);
  not not_31 (not_31_out, B3);
  not not_32 (not_32_out, B2);
  not not_33 (not_33_out, B1);
  not not_34 (not_34_out, B0);
  not not_35 (not_35_out, B3);
  not not_36 (not_36_out, B2);
  not not_37 (not_37_out, B2);
  not not_38 (not_38_out, B1);
  and and_1 (and_1_out, not_1_out, not_2_out, B1, not_3_out);
  and and_2 (and_2_out, B2, not_4_out, not_5_out);
  and and_3 (and_3_out, not_6_out, B2, B1, B0);
  and and_4 (and_4_out, B3, not_7_out, not_8_out);
  and and_5 (and_5_out, B3, not_9_out, B0);
  and and_6 (and_6_out, B3, B2, not_10_out);
  and and_7 (and_7_out, not_11_out, not_12_out, not_13_out);
  and and_8 (and_8_out, not_14_out, B1, not_15_out);
  and and_9 (and_9_out, not_16_out, B1, B0);
  and and_10 (and_10_out, not_17_out, B2, not_18_out, B0);
  and and_11 (and_11_out, B3, not_19_out, not_20_out);
  and and_12 (and_12_out, not_21_out, not_22_out, not_23_out);
  and and_13 (and_13_out, not_24_out, not_25_out, not_26_out);
  and and_14 (and_14_out, not_27_out, B2, B1);
  and and_15 (and_15_out, B2, B1, not_28_out);
  and and_16 (and_16_out, B3, not_29_out, B1, B0);
  and and_17 (and_17_out, B3, B2, not_30_out, B0);
  and and_18 (and_18_out, not_31_out, not_32_out, not_33_out, not_34_out);
  and and_19 (and_19_out, not_35_out, B1, B0);
  and and_20 (and_20_out, B3, not_36_out, B0);
  and and_21 (and_21_out, B3, not_37_out, B1);
  and and_22 (and_22_out, B3, B2, not_38_out);
  or or_1 (b3_2, and_1_out, and_2_out, and_3_out, and_4_out, and_5_out, and_6_out);
  or or_2 (b2_2, and_7_out, and_8_out, and_9_out, and_10_out, and_11_out);
  or or_3 (b1_2, and_12_out, and_13_out, and_14_out, and_15_out, and_16_out, and_17_out);
  or or_4 (b0_2, and_18_out, and_19_out, and_20_out, and_21_out, and_22_out);
endmodule

module S7 (
  input  B3,
  input  B2,
  input  B1,
  input  B0,
  output b3_2,
  output b2_2,
  output b1_2,
  output b0_2
);

  wire and_1_out, and_2_out, and_3_out, and_4_out, and_5_out, and_6_out, and_7_out, and_8_out, and_9_out,
       and_10_out, and_11_out, and_12_out, and_13_out, and_14_out, and_15_out, and_16_out, and_17_out,
       and_18_out, and_19_out, and_20_out, and_21_out, and_22_out, not_1_out, not_2_out, not_3_out,
       not_4_out, not_5_out, not_6_out, not_7_out, not_8_out, not_9_out, not_10_out, not_11_out, not_12_out,
       not_13_out, not_14_out, not_15_out, not_16_out, not_17_out, not_18_out, not_19_out, not_20_out,
       not_21_out, not_22_out, not_23_out, not_24_out, not_25_out, not_26_out, not_27_out, not_28_out,
       not_29_out, not_30_out, not_31_out, not_32_out, not_33_out, not_34_out, not_35_out, not_36_out,
       not_37_out;

  not not_1 (not_1_out, B3);
  and and_1 (and_1_out, not_1_out, not_2_out, B0);
  not not_2 (not_2_out, B1);
  not not_3 (not_3_out, B2);
  and and_2 (and_2_out, not_3_out, B1, not_4_out);
  not not_4 (not_4_out, B0);
  and and_3 (and_3_out, B2, not_5_out, not_6_out);
  not not_5 (not_5_out, B1);
  not not_6 (not_6_out, B0);
  not not_7 (not_7_out, B3);
  and and_4 (and_4_out, not_7_out, B2, B0);
  not not_8 (not_8_out, B2);
  and and_5 (and_5_out, B3, not_8_out, B1);
  not not_9 (not_9_out, B2);
  not not_10 (not_10_out, B1);
  not not_11 (not_11_out, B2);
  not not_12 (not_12_out, B0);
  not not_13 (not_13_out, B3);
  not not_14 (not_14_out, B1);
  not not_15 (not_15_out, B0);
  not not_16 (not_16_out, B2);
  not not_17 (not_17_out, B1);
  not not_18 (not_18_out, B3);
  not not_19 (not_19_out, B0);
  not not_20 (not_20_out, B3);
  not not_21 (not_21_out, B0);
  not not_22 (not_22_out, B3);
  not not_23 (not_23_out, B2);
  not not_24 (not_24_out, B1);
  not not_25 (not_25_out, B0);
  not not_26 (not_26_out, B3);
  not not_27 (not_27_out, B2);
  not not_28 (not_28_out, B1);
  not not_29 (not_29_out, B3);
  not not_30 (not_30_out, B2);
  not not_31 (not_31_out, B0);
  not not_32 (not_32_out, B2);
  not not_33 (not_33_out, B1);
  not not_34 (not_34_out, B0);
  not not_35 (not_35_out, B3);
  not not_36 (not_36_out, B1);
  not not_37 (not_37_out, B0);
  or or_1 (b3_2, and_1_out, and_2_out, and_3_out, and_4_out, and_5_out);
  and and_6 (and_6_out, not_9_out, not_10_out, B0);
  and and_7 (and_7_out, not_11_out, B1, not_12_out);
  and and_8 (and_8_out, not_13_out, B2, not_14_out, not_15_out);
  and and_9 (and_9_out, B3, not_16_out, not_17_out);
  and and_10 (and_10_out, B3, B2, B1);
  and and_11 (and_11_out, not_18_out, B1, not_19_out);
  and and_12 (and_12_out, not_20_out, B2, not_21_out);
  and and_13 (and_13_out, not_22_out, B2, B1);
  and and_14 (and_14_out, B3, not_23_out, not_24_out, not_25_out);
  and and_15 (and_15_out, B3, B1, B0);
  and and_16 (and_16_out, B3, B2, B0);
  and and_17 (and_17_out, not_26_out, not_27_out, not_28_out);
  and and_18 (and_18_out, not_29_out, not_30_out, not_31_out);
  and and_19 (and_19_out, not_32_out, not_33_out, not_34_out);
  and and_20 (and_20_out, not_35_out, B2, B1, B0);
  and and_21 (and_21_out, B3, B2, not_36_out);
  and and_22 (and_22_out, B3, B2, not_37_out);
  or or_2 (b2_2, and_6_out, and_7_out, and_8_out, and_9_out, and_10_out);
  or or_3 (b1_2, and_11_out, and_12_out, and_13_out, and_14_out, and_15_out, and_16_out);
  or or_4 (b0_2, and_17_out, and_18_out, and_19_out, and_20_out, and_21_out, and_22_out);
endmodule

module Rotate (
  input  [31:0] MSB_79__48,
  input  [31:0] MSB_47__16,
  input  [15:0] _15__LSB_0,
  output out_4,
  output out_5,
  output out_6,
  output out_7,
  output out_8,
  output out_9,
  output out_10,
  output out_11,
  output out_12,
  output out_13,
  output out_14,
  output out_15,
  output out_16,
  output out_17,
  output out_18,
  output out_19,
  output out_20,
  output out_21,
  output out_22,
  output out_23,
  output out_24,
  output out_25,
  output out_26,
  output out_27,
  output out_28,
  output out_29,
  output out_30,
  output out_31,
  output out_32,
  output out_33,
  output out_34,
  output out_35,
  output out_36,
  output out_37,
  output out_38,
  output out_39,
  output out_40,
  output out_41,
  output out_42,
  output out_43,
  output out_44,
  output out_45,
  output out_46,
  output out_47,
  output out_48,
  output out_49,
  output out_50,
  output out_51,
  output out_52,
  output out_53,
  output out_54,
  output out_55,
  output out_56,
  output out_57,
  output out_58,
  output out_59,
  output out_60,
  output out_61,
  output out_62,
  output out_63,
  output out_64,
  output out_65,
  output out_66,
  output out_67,
  output out_68,
  output out_69,
  output out_70,
  output out_71,
  output out_72,
  output out_73,
  output out_74,
  output out_75,
  output out_76,
  output out_77,
  output out_78,
  output out_79,
  output out_80,
  output out_81,
  output out_82,
  output out_83
);


  assign out_4 = MSB_79__48[18];
  assign out_5 = MSB_79__48[17];
  assign out_6 = MSB_79__48[16];
  assign out_7 = MSB_79__48[15];
  assign out_8 = MSB_79__48[14];
  assign out_9 = MSB_79__48[13];
  assign out_10 = MSB_79__48[12];
  assign out_11 = MSB_79__48[11];
  assign out_12 = MSB_79__48[10];
  assign out_13 = MSB_79__48[9];
  assign out_14 = MSB_79__48[8];
  assign out_15 = MSB_79__48[7];
  assign out_16 = MSB_79__48[6];
  assign out_17 = MSB_79__48[5];
  assign out_18 = MSB_79__48[4];
  assign out_19 = MSB_79__48[3];
  assign out_20 = MSB_79__48[2];
  assign out_21 = MSB_79__48[1];
  assign out_22 = MSB_79__48[0];
  assign out_23 = MSB_47__16[31];
  assign out_24 = MSB_47__16[30];
  assign out_25 = MSB_47__16[29];
  assign out_26 = MSB_47__16[28];
  assign out_27 = MSB_47__16[27];
  assign out_28 = MSB_47__16[26];
  assign out_29 = MSB_47__16[25];
  assign out_30 = MSB_47__16[24];
  assign out_31 = MSB_47__16[23];
  assign out_32 = MSB_47__16[22];
  assign out_33 = MSB_47__16[21];
  assign out_34 = MSB_47__16[20];
  assign out_35 = MSB_47__16[19];
  assign out_36 = MSB_47__16[18];
  assign out_37 = MSB_47__16[17];
  assign out_38 = MSB_47__16[16];
  assign out_39 = MSB_47__16[15];
  assign out_40 = MSB_47__16[14];
  assign out_41 = MSB_47__16[13];
  assign out_42 = MSB_47__16[12];
  assign out_43 = MSB_47__16[11];
  assign out_44 = MSB_47__16[10];
  assign out_45 = MSB_47__16[9];
  assign out_46 = MSB_47__16[8];
  assign out_47 = MSB_47__16[7];
  assign out_48 = MSB_47__16[6];
  assign out_49 = MSB_47__16[5];
  assign out_50 = MSB_47__16[4];
  assign out_51 = MSB_47__16[3];
  assign out_52 = MSB_47__16[2];
  assign out_53 = MSB_47__16[1];
  assign out_54 = MSB_47__16[0];
  assign out_55 = _15__LSB_0[15];
  assign out_56 = _15__LSB_0[14];
  assign out_57 = _15__LSB_0[13];
  assign out_58 = _15__LSB_0[12];
  assign out_59 = _15__LSB_0[11];
  assign out_60 = _15__LSB_0[10];
  assign out_61 = _15__LSB_0[9];
  assign out_62 = _15__LSB_0[8];
  assign out_63 = _15__LSB_0[7];
  assign out_64 = _15__LSB_0[6];
  assign out_65 = _15__LSB_0[5];
  assign out_66 = _15__LSB_0[4];
  assign out_67 = _15__LSB_0[3];
  assign out_68 = _15__LSB_0[2];
  assign out_69 = _15__LSB_0[1];
  assign out_70 = _15__LSB_0[0];
  assign out_71 = MSB_79__48[31];
  assign out_72 = MSB_79__48[30];
  assign out_73 = MSB_79__48[29];
  assign out_74 = MSB_79__48[28];
  assign out_75 = MSB_79__48[27];
  assign out_76 = MSB_79__48[26];
  assign out_77 = MSB_79__48[25];
  assign out_78 = MSB_79__48[24];
  assign out_79 = MSB_79__48[23];
  assign out_80 = MSB_79__48[22];
  assign out_81 = MSB_79__48[21];
  assign out_82 = MSB_79__48[20];
  assign out_83 = MSB_79__48[19];
endmodule
