// Logisim project PRESENT.circ as structural Verilog: 12 circuits, main circuit main
module main (
  output [31:0] L_Out,
  output [31:0] R_Out,
  output halt
);

  wire and_1_out, clock_1_out, nand_1_out, not_1_out, or_1_out;
  wire [1:0] counter_1_q;
  wire [4:0] adder_1_out, counter_2_q;
  wire [15:0] keytransform_1__15__lsb_0__out, multiplexer_3_out, register_3_q;
  wire [31:0] addroundkey_f_1_out_5, addroundkey_f_1_out_6, keytransform_1_msb_47__16__out,
       keytransform_1_msb_79__48__out, multiplexer_1_out, multiplexer_2_out, multiplexer_4_out,
       multiplexer_5_out, ram_1_data, ram_2_data, ram_3_data, ram_4_data, ram_5_data, register_1_q,
       register_2_q, register_4_q, register_5_q, sprlayer_f_1_output, sprlayer_f_1_output_2;

  RAM #(.addrWidth(3), .dataWidth(32)) ram_1 (
    .addr(3'b100), .data(ram_1_data), .clk(clock_1_out), .ld(1'b1));  // open: sel, clr
  RAM #(.addrWidth(3), .dataWidth(32)) ram_2 (
    .addr(3'b011), .data(ram_2_data), .clk(clock_1_out), .ld(1'b1));  // open: sel, clr
  RAM #(.addrWidth(3), .dataWidth(32)) ram_3 (
    .addr(3'b010), .data(ram_3_data), .clk(clock_1_out), .ld(1'b1));  // open: sel, clr
  RAM #(.addrWidth(3), .dataWidth(32)) ram_4 (
    .addr(3'b001), .data(ram_4_data), .clk(clock_1_out), .ld(1'b1));  // open: sel, clr
  RAM #(.addrWidth(3), .dataWidth(32)) ram_5 (
    .addr(3'b000), .data(ram_5_data), .clk(clock_1_out), .ld(1'b1));  // open: sel, clr
  Clock clock_1 (.out(clock_1_out));
  Counter #(.width(2), .max('h3), .ongoal("stay")) counter_1 (
    .Q(counter_1_q), .clk(clock_1_out));  // open: load, D, count, carry, clr
  AddRoundKey_F addroundkey_f_1 (
    .in_1({ram_1_data[15:0], ram_2_data[31:16]}), .in_2({ram_2_data[15:0], ram_3_data[31:16]}),
    .in_3(ram_4_data), .in_4(ram_5_data), .out_5(addroundkey_f_1_out_5), .out_6(addroundkey_f_1_out_6));
  and and_1 (and_1_out, counter_1_q[0], counter_1_q[1], clock_1_out);
  Counter #(.width(5), .max('h1f), .ongoal("stay")) counter_2 (
    .Q(counter_2_q), .carry(halt), .clk(and_1_out));  // open: load, D, count, clr
  Multiplexer #(.width(32), .enable("false")) multiplexer_1 (
    .in0({ram_1_data[15:0], ram_2_data[31:16]}), .in1(register_1_q), .out(multiplexer_1_out), .sel(or_1_out));
  Multiplexer #(.width(32), .enable("false")) multiplexer_2 (
    .in0({ram_2_data[15:0], ram_3_data[31:16]}), .in1(register_2_q), .out(multiplexer_2_out), .sel(or_1_out));
  Multiplexer #(.width(16), .enable("false")) multiplexer_3 (
    .in0(ram_3_data[15:0]), .in1(register_3_q), .out(multiplexer_3_out), .sel(or_1_out));
  Multiplexer #(.width(32), .enable("false")) multiplexer_4 (
    .in0(addroundkey_f_1_out_5), .in1(register_4_q), .out(multiplexer_4_out), .sel(or_1_out));
  Multiplexer #(.width(32), .enable("false")) multiplexer_5 (
    .in0(addroundkey_f_1_out_6), .in1(register_5_q), .out(multiplexer_5_out), .sel(or_1_out));
  or or_1 (or_1_out, counter_2_q[0], counter_2_q[1], counter_2_q[2], counter_2_q[3], counter_2_q[4]);
  KeyTransform keytransform_1 (
    .MSB_79__48(multiplexer_1_out), .MSB_47__16(multiplexer_2_out), ._15__LSB_0(multiplexer_3_out),
    .in_4(adder_1_out), .MSB_79__48__Out(keytransform_1_msb_79__48__out),
    .MSB_47__16__Out(keytransform_1_msb_47__16__out), ._15__LSB_0__Out(keytransform_1__15__lsb_0__out));
  SPRLayer_F sprlayer_f_1 (
    .Key(keytransform_1_msb_79__48__out), .Key_2(keytransform_1_msb_47__16__out), .Cipher(multiplexer_4_out),
    .Cipher_2(multiplexer_5_out), .Output(sprlayer_f_1_output), .Output_2(sprlayer_f_1_output_2));
  Adder #(.width(5)) adder_1 (.a(counter_2_q), .b(5'b00001), .out(adder_1_out));  // open: cin, cout
  nand nand_1 (nand_1_out, counter_2_q[0], counter_2_q[1], counter_2_q[2], counter_2_q[3], counter_2_q[4]);
  Register #(.width(32)) register_1 (
    .D(keytransform_1_msb_79__48__out), .en(nand_1_out), .Q(register_1_q), .clk(and_1_out));  // open: clr
  Register #(.width(32)) register_2 (
    .D(keytransform_1_msb_47__16__out), .en(nand_1_out), .Q(register_2_q), .clk(and_1_out));  // open: clr
  Register #(.width(16)) register_3 (
    .D(keytransform_1__15__lsb_0__out), .en(nand_1_out), .Q(register_3_q), .clk(and_1_out));  // open: clr
  Register #(.width(32)) register_4 (
    .D(sprlayer_f_1_output), .en(nand_1_out), .Q(register_4_q), .clk(and_1_out));  // open: clr
  Register #(.width(32)) register_5 (
    .D(sprlayer_f_1_output_2), .en(nand_1_out), .Q(register_5_q), .clk(and_1_out));  // open: clr
  not not_1 (not_1_out, nand_1_out);
  assign L_Out = not_1_out ? register_4_q : 32'bz;  // Controlled_Buffer controlled_buffer_1
  assign R_Out = not_1_out ? register_5_q : 32'bz;  // Controlled_Buffer controlled_buffer_2
  // Probe on L_Out
  // Probe on R_Out

  // Notes on the sheet:
  //   16MSBKEY
  //   32MIDDKE MSB KEY
  //   32LSB KEY
  //   32MSB PLAINTEXT
  //   32LSB  PLAINTEXT
endmodule

module SBoxA (
  input  in_1,
  input  in_2,
  input  in_3,
  input  in_4,
  output out_5
);

  wire and_1_out, and_2_out, and_3_out, and_4_out, and_5_out, not_1_out, not_2_out, not_3_out, not_4_out;

  not not_1 (not_1_out, in_1);
  not not_2 (not_2_out, in_2);
  not not_3 (not_3_out, in_3);
  not not_4 (not_4_out, in_4);
  and and_1 (and_1_out, not_1_out, not_3_out, not_4_out);
  and and_2 (and_2_out, not_1_out, in_3, in_4);
  and and_3 (and_3_out, not_1_out, in_2, not_4_out);
  and and_4 (and_4_out, in_1, not_2_out, in_4);
  and and_5 (and_5_out, in_1, not_2_out, in_3);
  or or_1 (out_5, and_5_out, and_1_out, and_2_out, and_3_out, and_4_out);
endmodule

module SBoxB (
  input  in_1,
  input  in_2,
  input  in_3,
  input  in_4,
  output out_5
);

  wire and_1_out, and_2_out, and_3_out, and_4_out, and_5_out, not_1_out, not_2_out, not_3_out, not_4_out;

  not not_1 (not_1_out, in_1);
  not not_2 (not_2_out, in_2);
  not not_3 (not_3_out, in_3);
  not not_4 (not_4_out, in_4);
  and and_1 (and_1_out, not_1_out, not_2_out, not_3_out);
  and and_2 (and_2_out, not_2_out, not_3_out, in_4);
  and and_3 (and_3_out, not_2_out, in_3, not_4_out);
  and and_4 (and_4_out, in_1, in_1, in_2, not_3_out);
  and and_5 (and_5_out, not_1_out, in_2, in_3, in_4);
  or or_1 (out_5, and_5_out, and_1_out, and_2_out, and_3_out, and_4_out);
endmodule

module SBoxC (
  input  in_1,
  input  in_2,
  input  in_3,
  input  in_4,
  output out_5
);

  wire and_1_out, and_2_out, and_3_out, and_4_out, and_5_out, not_1_out, not_2_out, not_3_out, not_4_out;

  not not_1 (not_1_out, in_1);
  not not_2 (not_2_out, in_2);
  not not_3 (not_3_out, in_3);
  not not_4 (not_4_out, in_4);
  and and_1 (and_1_out, not_1_out, not_2_out, not_2_out, in_3);
  and and_2 (and_2_out, not_1_out, in_3, not_4_out);
  and and_3 (and_3_out, not_2_out, in_3, not_4_out);
  and and_4 (and_4_out, in_1, in_1, not_2_out, not_3_out);
  and and_5 (and_5_out, in_1, in_2, in_4);
  or or_1 (out_5, and_5_out, and_1_out, and_2_out, and_3_out, and_4_out);
endmodule

module SBoxD (
  input  in_1,
  input  in_2,
  input  in_3,
  input  in_4,
  output out_5
);

  wire and_1_out, and_2_out, and_3_out, and_4_out, and_5_out, and_6_out, not_1_out, not_2_out, not_3_out,
       not_4_out, or_1_out;

  not not_1 (not_1_out, in_1);
  not not_2 (not_2_out, in_2);
  not not_3 (not_3_out, in_3);
  not not_4 (not_4_out, in_4);
  and and_1 (and_1_out, not_1_out, not_2_out, in_4, in_4);
  and and_2 (and_2_out, not_1_out, in_3, in_4);
  and and_3 (and_3_out, in_1, not_2_out, not_4_out);
  and and_4 (and_4_out, in_1, in_3, not_4_out);
  and and_5 (and_5_out, not_1_out, in_2, not_3_out, not_4_out);
  and and_6 (and_6_out, in_1, in_2, not_3_out, in_4);
  or or_1 (or_1_out, and_5_out, and_6_out);
  or or_2 (out_5, or_1_out, and_1_out, and_2_out, and_3_out, and_4_out);
endmodule

module XOR5 (
  input  in_1,
  input  in_2,
  input  in_3,
  input  in_4,
  input  in_5,
  input  in_6,
  input  in_7,
  input  in_8,
  input  in_9,
  input  in_10,
  output out_11,
  output out_12,
  output out_13,
  output out_14,
  output out_15
);

  xor xor_1 (out_11, in_1, in_6);
  xor xor_2 (out_12, in_2, in_7);
  xor xor_3 (out_13, in_3, in_8);
  xor xor_4 (out_14, in_4, in_9);
  xor xor_5 (out_15, in_5, in_10);
endmodule

module AddRoundKey_F (
  input  [31:0] in_1,
  input  [31:0] in_2,
  input  [31:0] in_3,
  input  [31:0] in_4,
  output [31:0] out_5,
  output [31:0] out_6
);

  assign out_5 = in_1 ^ in_3;  // XOR_Gate xor_1, 32 bits wide
  assign out_6 = in_2 ^ in_4;  // XOR_Gate xor_2, 32 bits wide
endmodule

module PBox_F (
  input  [31:0] MSB,
  input  [31:0] LSB,
  output [31:0] MSB_Output,
  output [31:0] LSB_Output
);


  assign LSB_Output = {MSB[29], MSB[25], MSB[21], MSB[17], MSB[13], MSB[9], MSB[5], MSB[1], LSB[29], LSB[25], LSB[21], LSB[17], LSB[13], LSB[9], LSB[5], LSB[1], MSB[28], MSB[24], MSB[20], MSB[16], MSB[12], MSB[8], MSB[4], MSB[0], LSB[28], LSB[24], LSB[20], LSB[16], LSB[12], LSB[8], LSB[4], LSB[0]};
  assign MSB_Output = {MSB[31], MSB[27], MSB[23], MSB[19], MSB[15], MSB[11], MSB[7], MSB[3], LSB[31], LSB[27], LSB[23], LSB[19], LSB[15], LSB[11], LSB[7], LSB[3], MSB[30], MSB[26], MSB[22], MSB[18], MSB[14], MSB[10], MSB[6], MSB[2], LSB[30], LSB[26], LSB[22], LSB[18], LSB[14], LSB[10], LSB[6], LSB[2]};

  // Other names for the same wires on the sheet: _0 = LSB[0]; _1 = LSB[4]; _2 = LSB[8]; _3 = LSB[12]; _4 = LSB[16];
  //   _5 = LSB[20]; _6 = LSB[24]; _7 = LSB[28]; _8 = MSB[0]; _9 = MSB[4]; _10 = MSB[8]; _11 = MSB[12]; _12 = MSB[16];
  //   _13 = MSB[20]; _14 = MSB[24]; _15 = MSB[28]; _16 = LSB[1]; _17 = LSB[5]; _18 = LSB[9]; _19 = LSB[13];
  //   _20 = LSB[17]; _21 = LSB[21]; _22 = LSB[25]; _23 = LSB[29]; _24 = MSB[1]; _25 = MSB[5]; _26 = MSB[9];
  //   _27 = MSB[13]; _28 = MSB[17]; _29 = MSB[21]; _30 = MSB[25]; _31 = MSB[29]; _32 = LSB[2]; _33 = LSB[6];
  //   _34 = LSB[10]; _35 = LSB[14]; _36 = LSB[18]; _37 = LSB[22]; _38 = LSB[26]; _39 = LSB[30]; _40 = MSB[2];
  //   _41 = MSB[6]; _42 = MSB[10]; _43 = MSB[14]; _44 = MSB[18]; _45 = MSB[22]; _46 = MSB[26]; _47 = MSB[30];
  //   _48 = LSB[3]; _49 = LSB[7]; _50 = LSB[11]; _51 = LSB[15]; _52 = LSB[19]; _53 = LSB[23]; _54 = LSB[27];
  //   _55 = LSB[31]; _56 = MSB[3]; _57 = MSB[7]; _58 = MSB[11]; _59 = MSB[15]; _60 = MSB[19]; _61 = MSB[23];
  //   _62 = MSB[27]; _63 = MSB[31]
endmodule

module SBox4Bit_F (
  input  in_1,
  input  in_2,
  input  in_3,
  input  in_4,
  output out_5,
  output out_6,
  output out_7,
  output out_8
);

  SBoxA sboxa_1 (.in_1(in_1), .in_2(in_2), .in_3(in_3), .in_4(in_4), .out_5(out_5));
  SBoxB sboxb_1 (.in_1(in_1), .in_2(in_2), .in_3(in_3), .in_4(in_4), .out_5(out_6));
  SBoxC sboxc_1 (.in_1(in_1), .in_2(in_2), .in_3(in_3), .in_4(in_4), .out_5(out_7));
  SBoxD sboxd_1 (.in_1(in_1), .in_2(in_2), .in_3(in_3), .in_4(in_4), .out_5(out_8));
endmodule

module SBox64Bit_F (
  input  [31:0] in_1,
  input  [31:0] in_2,
  output [31:0] out_3,
  output [31:0] out_4
);

  SBox4Bit_F sbox4bit_f_1 (
    .in_1(in_1[31]), .in_2(in_1[30]), .in_3(in_1[29]), .in_4(in_1[28]), .out_5(out_3[31]), .out_6(out_3[30]),
    .out_7(out_3[29]), .out_8(out_3[28]));
  SBox4Bit_F sbox4bit_f_2 (
    .in_1(in_1[27]), .in_2(in_1[26]), .in_3(in_1[25]), .in_4(in_1[24]), .out_5(out_3[27]), .out_6(out_3[26]),
    .out_7(out_3[25]), .out_8(out_3[24]));
  SBox4Bit_F sbox4bit_f_3 (
    .in_1(in_1[23]), .in_2(in_1[22]), .in_3(in_1[21]), .in_4(in_1[20]), .out_5(out_3[23]), .out_6(out_3[22]),
    .out_7(out_3[21]), .out_8(out_3[20]));
  SBox4Bit_F sbox4bit_f_4 (
    .in_1(in_1[19]), .in_2(in_1[18]), .in_3(in_1[17]), .in_4(in_1[16]), .out_5(out_3[19]), .out_6(out_3[18]),
    .out_7(out_3[17]), .out_8(out_3[16]));
  SBox4Bit_F sbox4bit_f_5 (
    .in_1(in_1[15]), .in_2(in_1[14]), .in_3(in_1[13]), .in_4(in_1[12]), .out_5(out_3[15]), .out_6(out_3[14]),
    .out_7(out_3[13]), .out_8(out_3[12]));
  SBox4Bit_F sbox4bit_f_6 (
    .in_1(in_1[11]), .in_2(in_1[10]), .in_3(in_1[9]), .in_4(in_1[8]), .out_5(out_3[11]), .out_6(out_3[10]),
    .out_7(out_3[9]), .out_8(out_3[8]));
  SBox4Bit_F sbox4bit_f_7 (
    .in_1(in_1[7]), .in_2(in_1[6]), .in_3(in_1[5]), .in_4(in_1[4]), .out_5(out_3[7]), .out_6(out_3[6]),
    .out_7(out_3[5]), .out_8(out_3[4]));
  SBox4Bit_F sbox4bit_f_8 (
    .in_1(in_1[3]), .in_2(in_1[2]), .in_3(in_1[1]), .in_4(in_1[0]), .out_5(out_3[3]), .out_6(out_3[2]),
    .out_7(out_3[1]), .out_8(out_3[0]));
  SBox4Bit_F sbox4bit_f_9 (
    .in_1(in_2[31]), .in_2(in_2[30]), .in_3(in_2[29]), .in_4(in_2[28]), .out_5(out_4[31]), .out_6(out_4[30]),
    .out_7(out_4[29]), .out_8(out_4[28]));
  SBox4Bit_F sbox4bit_f_10 (
    .in_1(in_2[27]), .in_2(in_2[26]), .in_3(in_2[25]), .in_4(in_2[24]), .out_5(out_4[27]), .out_6(out_4[26]),
    .out_7(out_4[25]), .out_8(out_4[24]));
  SBox4Bit_F sbox4bit_f_11 (
    .in_1(in_2[23]), .in_2(in_2[22]), .in_3(in_2[21]), .in_4(in_2[20]), .out_5(out_4[23]), .out_6(out_4[22]),
    .out_7(out_4[21]), .out_8(out_4[20]));
  SBox4Bit_F sbox4bit_f_12 (
    .in_1(in_2[19]), .in_2(in_2[18]), .in_3(in_2[17]), .in_4(in_2[16]), .out_5(out_4[19]), .out_6(out_4[18]),
    .out_7(out_4[17]), .out_8(out_4[16]));
  SBox4Bit_F sbox4bit_f_13 (
    .in_1(in_2[15]), .in_2(in_2[14]), .in_3(in_2[13]), .in_4(in_2[12]), .out_5(out_4[15]), .out_6(out_4[14]),
    .out_7(out_4[13]), .out_8(out_4[12]));
  SBox4Bit_F sbox4bit_f_14 (
    .in_1(in_2[11]), .in_2(in_2[10]), .in_3(in_2[9]), .in_4(in_2[8]), .out_5(out_4[11]), .out_6(out_4[10]),
    .out_7(out_4[9]), .out_8(out_4[8]));
  SBox4Bit_F sbox4bit_f_15 (
    .in_1(in_2[7]), .in_2(in_2[6]), .in_3(in_2[5]), .in_4(in_2[4]), .out_5(out_4[7]), .out_6(out_4[6]),
    .out_7(out_4[5]), .out_8(out_4[4]));
  SBox4Bit_F sbox4bit_f_16 (
    .in_1(in_2[3]), .in_2(in_2[2]), .in_3(in_2[1]), .in_4(in_2[0]), .out_5(out_4[3]), .out_6(out_4[2]),
    .out_7(out_4[1]), .out_8(out_4[0]));
endmodule

module SPRLayer_F (
  input  [31:0] Key,
  input  [31:0] Key_2,
  input  [31:0] Cipher,
  input  [31:0] Cipher_2,
  output [31:0] Output,
  output [31:0] Output_2
);

  wire [31:0] pbox_f_1_lsb_output, pbox_f_1_msb_output, sbox64bit_f_1_out_3, sbox64bit_f_1_out_4;

  SBox64Bit_F sbox64bit_f_1 (.in_1(Cipher), .in_2(Cipher_2), .out_3(sbox64bit_f_1_out_3), .out_4(sbox64bit_f_1_out_4));
  PBox_F pbox_f_1 (
    .MSB(sbox64bit_f_1_out_3), .LSB(sbox64bit_f_1_out_4), .MSB_Output(pbox_f_1_msb_output),
    .LSB_Output(pbox_f_1_lsb_output));
  AddRoundKey_F addroundkey_f_1 (
    .in_1(Key), .in_2(Key_2), .in_3(pbox_f_1_msb_output), .in_4(pbox_f_1_lsb_output), .out_5(Output),
    .out_6(Output_2));
endmodule

module KeyTransform (
  input  [31:0] MSB_79__48,
  input  [31:0] MSB_47__16,
  input  [15:0] _15__LSB_0,
  input  [4:0] in_4,
  output [31:0] MSB_79__48__Out,
  output [31:0] MSB_47__16__Out,
  output [15:0] _15__LSB_0__Out
);

  SBox4Bit_F sbox4bit_f_1 (
    .in_1(MSB_47__16[2]), .in_2(MSB_47__16[1]), .in_3(MSB_47__16[0]), .in_4(_15__LSB_0[15]),
    .out_5(MSB_79__48__Out[31]), .out_6(MSB_79__48__Out[30]), .out_7(MSB_79__48__Out[29]),
    .out_8(MSB_79__48__Out[28]));
  assign {MSB_47__16__Out[3:0], _15__LSB_0__Out[15]} = MSB_47__16[22:18] ^ in_4;  // XOR_Gate xor_1, 5 bits wide

  assign _15__LSB_0__Out[14:0] = MSB_47__16[17:3];
  assign MSB_47__16__Out[31:4] = {MSB_79__48[18:0], MSB_47__16[31:23]};
  assign MSB_79__48__Out[27:0] = {_15__LSB_0[14:0], MSB_79__48[31:19]};
endmodule
